// Logisim project CS_Final.circ as structural Verilog: 15 circuits, main circuit main
module main (
  input  in_1,
  input  in_2,
  output [5:0] out_3,
  output [5:0] out_4,
  output [9:0] reg_0,
  output [9:0] out_6,
  output [9:0] reg_1,
  output [9:0] out_8,
  output [9:0] reg_2,
  output [9:0] reg_3,
  output [9:0] reg_4,
  output [9:0] reg_5,
  output [9:0] reg_6,
  output [9:0] reg_7,
  output [9:0] out_15,
  output [9:0] reg_8,
  output [9:0] reg_9,
  output [9:0] reg_10,
  output [9:0] reg_11,
  output [9:0] reg_12,
  output [9:0] reg_13,
  output [9:0] reg_14,
  output [9:0] reg_15,
  output [9:0] out_24,
  output [9:0] out_25,
  output [9:0] out_26,
  output [9:0] out_27,
  output [9:0] out_28,
  output [9:0] out_29,
  output [9:0] out_30,
  output [9:0] out_31,
  output [9:0] out_32,
  output [9:0] out_33,
  output [9:0] out_34,
  output [9:0] out_35,
  output [9:0] out_36,
  output zero_flag,
  output [9:0] out_38,
  output overflow_flag,
  output [9:0] out_40,
  output [9:0] out_41,
  output carry_flag,
  output [9:0] out_43,
  output [9:0] out_44,
  output sign_flag,
  output [9:0] out_46,
  output [9:0] out_47,
  output [9:0] out_48,
  output [9:0] out_49,
  output [9:0] out_50,
  output [9:0] out_51,
  output [9:0] out_52,
  output [9:0] out_53,
  output [9:0] out_54,
  output [9:0] out_55,
  output [9:0] out_56,
  output [9:0] out_57,
  output [9:0] out_58,
  output [9:0] out_59,
  output [9:0] out_60,
  output [9:0] out_61,
  output [9:0] out_62,
  output [9:0] out_63,
  output [9:0] out_64,
  output [5:0] out_65,
  output [9:0] out_66,
  output [3:0] out_67,
  output [9:0] out_68,
  output [9:0] out_69,
  output [9:0] out_70,
  output [5:0] out_71,
  output [9:0] out_72,
  output [9:0] out_73,
  output [9:0] out_74,
  output [9:0] out_75,
  output [9:0] out_76,
  output [9:0] out_77,
  output [9:0] out_78,
  output [9:0] out_79,
  output [9:0] out_80,
  output [9:0] out_81,
  output [9:0] out_82,
  output [9:0] out_83,
  output [9:0] out_84,
  output [9:0] out_85,
  output [9:0] out_86
);

  wire a_in, a_out, alu_out, alu_sub, amount_in, b_in, b_out, clk, flag_clk, ins_reg_in_en, ins_reg_out_en,
       mar_in_en, pc_en, pc_in_en, pc_out, pull_resistor_2_node, ram_rd, rotate_in, rotate_out, shift_in,
       shift_out, sram_rd, sram_wr;
  wire [9:6] reg_gp_3_reg_int_out;
  wire [9:9] pull_resistor_1_node;

  sram sram_1 (
    .sram_d_in(out_41), .sram_wr(sram_wr), .sram_rd(sram_rd), .mar_d_in(out_41), .mar_in_en(mar_in_en),
    .sram_clk(clk), .sram_d_out(out_41), .out_8(reg_0), .out_9(reg_1), .out_10(reg_2), .out_11(reg_3),
    .out_12(reg_4), .out_13(reg_5), .out_14(reg_6), .out_15(reg_7), .out_16(reg_8), .out_17(reg_9),
    .out_18(reg_10), .out_19(reg_11), .out_20(reg_12), .out_21(reg_13), .out_22(reg_14), .out_23(reg_15),
    .out_24(out_24), .out_25(out_27), .out_26(out_29), .out_27(out_30), .out_28(out_31), .out_29(out_32),
    .out_30(out_33), .out_31(out_34), .out_32(out_35), .out_33(out_36), .out_34(out_38), .out_35(out_40),
    .out_36(out_43), .out_37(out_44), .out_38(out_47), .out_39(out_48), .out_40(out_49), .out_41(out_50),
    .out_42(out_51), .out_43(out_53), .out_44(out_54), .out_45(out_55), .out_46(out_56), .out_47(out_57),
    .out_48(out_58), .out_49(out_59), .out_50(out_60), .out_51(out_63), .out_52(out_64), .out_53(out_66),
    .out_54(out_68), .out_55(out_69), .out_56(out_70), .out_57(out_72), .out_58(out_73), .out_59(out_74),
    .out_60(out_75), .out_61(out_76), .out_62(out_77), .out_63(out_78), .out_64(out_79), .out_65(out_80),
    .out_66(out_81), .out_67(out_82), .out_68(out_83), .out_69(out_84), .out_70(out_85), .out_71(out_86));
  assign out_41 = in_2 ? out_8 : 10'bz;  // Controlled_Buffer controlled_buffer_1
  Clock clock_1 (.out(clk));
  barrel_shifter barrel_shifter_1 (
    .shift_data(out_41), .shift_out_en(shift_out), .shift_in_en(shift_in), .clk(clk), .bit_amount(out_41),
    .shift_amount_in(amount_in), .shift_data_out(out_41));
  ring_rotator ring_rotator_1 (
    .rotate_data(out_41), .rotate_out_en(rotate_out), .rotate_in_en(rotate_in), .clk(clk),
    .bit_amount(out_41), .rotate_amount_in(amount_in), .rotate_data_out(out_41));
  pc_new pc_new_1 (
    .pc_en(pc_en), .pc_in(out_41[5:0]), .pc_in_en(pc_in_en), .pc_reset(in_1), .pc_clk(clk),
    .pc_out_en(pc_out), .pc_value(out_4), .pc_out(out_41[5:0]));
  assign out_15 = in_2 ? out_41 : 10'bz;  // Controlled_Buffer controlled_buffer_2
  reg_gp reg_gp_1 (
    .reg_in(out_41), .reg_in_en(a_in), .reg_clk(clk), .reg_out_en(a_out), .reg_int_out(out_25),
    .reg_out(out_41));
  reg_gp reg_gp_2 (
    .reg_in(out_41), .reg_in_en(b_in), .reg_clk(clk), .reg_out_en(b_out), .reg_int_out(out_52),
    .reg_out(out_41));
  ins_reg ins_reg_1 (
    .ins_reg_in(out_41), .ins_reg_in_en(ins_reg_in_en), .clk(clk), .ins_reg_out_en(ins_reg_out_en),
    .out_5(out_61), .add_outs(out_41[5:0]), .ins_out(out_67));
  // RGBLED rgbled_1: pin names not known; wires that end beside it: out_25[1], out_25[0], out_25[2]
  reg_gp reg_gp_3 (
    .reg_in(out_15), .reg_in_en(mar_in_en), .reg_clk(clk), .reg_int_out({reg_gp_3_reg_int_out, out_3}));  // open: reg_out_en, reg_out
  alu alu_1 (
    .alu_in_1(out_25), .alu_out_en(alu_out), .alu_sub(alu_sub), .alu_in_2(out_52), .alu_zero_out(zero_flag),
    .alu_overflow_out(overflow_flag), .alu_carry_out(carry_flag), .alu_out(out_41), .alu_sign_out(sign_flag));
  RAM #(.addrWidth(6), .dataWidth(10), .trigger("falling")) ram_1 (
    .addr(out_3), .oe(ram_rd), .clk(clk), .dout(out_6));  // open: we, din
  Pull_Resistor pull_resistor_1 (.node(pull_resistor_1_node[9]));
  cs cs_1 (
    .debug(in_2), .clk(clk), .ring_reset(in_1), .data_in(out_67), .flag_reg(out_26), .pc_en(pc_en),
    .pc_out(pc_out), .pc_reset(in_1), .sram_wr(sram_wr), .out_10(out_71), .sram_rd(sram_rd),
    .mar_in_en(mar_in_en), .ins_reg_in_en(ins_reg_in_en), .ins_reg_out_en(ins_reg_out_en), .a_in(a_in),
    .a_out(a_out), .alu_out(alu_out), .alu_sub(alu_sub), .b_in(b_in), .b_out(b_out), .ram_rd(ram_rd),
    .pc_in_en(pc_in_en), .flag_clk(flag_clk), .amount_in(amount_in), .shift_in(shift_in),
    .shift_out(shift_out), .rotate_in(rotate_in), .rotate_out(rotate_out));
  Pull_Resistor #(.pull(1)) pull_resistor_2 (.node(pull_resistor_2_node));
  assign out_8 = ram_rd ? out_6 : 10'bz;  // Controlled_Buffer controlled_buffer_3
  reg_gp flag_reg (
    .reg_in({{6{pull_resistor_1_node[9]}}, sign_flag, carry_flag, overflow_flag, zero_flag}),
    .reg_in_en(pull_resistor_2_node), .reg_clk(flag_clk), .reg_int_out(out_26));  // open: reg_out_en, reg_out

  assign out_28 = out_25;
  assign out_46 = out_41;
  assign out_62 = out_61;
  assign out_65 = out_41[5:0];

  // Other names for the same wires on the sheet: debug = in_2; debug_data[9:0] = out_8; debug_data_out[9:0] = out_41;
  //   flag_out[9:0] = out_26; pc_reset = in_1; ring_reset = in_1

  // Notes on the sheet:
  //   Clock
  //   Resets
  //   Debug & Testing
  //   Green: A=B
  //   Red: A>B
  //   Blue: A<B
  //   s c o z
  //   0. Debug
  //   1. LDA
  //   2. LDB
  //   3. OUT
  //   4. SUB
  //   5. HLT
  //   6. LDI
  //   7. STA
  //   8. CMP
  //   9. JMP
  //   10. JNZ
  //   11. JNC
  //   12. SFT
  //   13.RTE
endmodule

module reg_gp (
  input  [9:0] reg_in,
  input  reg_in_en,
  input  reg_clk,
  input  reg_out_en,
  output [9:0] reg_int_out,
  output [9:0] reg_out
);

  wire multiplexer_1_out, multiplexer_2_out, multiplexer_3_out, multiplexer_4_out, multiplexer_5_out,
       multiplexer_6_out, multiplexer_7_out, multiplexer_8_out, multiplexer_9_out, multiplexer_10_out;

  Multiplexer multiplexer_1 (.in0(reg_int_out[9]), .in1(reg_in[9]), .out(multiplexer_1_out), .sel(reg_in_en));
  D_Flip_Flop d_ff_1 (.D(multiplexer_1_out), .clk(reg_clk), .Q(reg_int_out[9]));  // open: Qn, preset, reset
  assign reg_out[9] = reg_out_en ? reg_int_out[9] : 1'bz;  // Controlled_Buffer controlled_buffer_1
  Multiplexer multiplexer_2 (.in0(reg_int_out[8]), .in1(reg_in[8]), .out(multiplexer_2_out), .sel(reg_in_en));
  D_Flip_Flop d_ff_2 (.D(multiplexer_2_out), .clk(reg_clk), .Q(reg_int_out[8]));  // open: Qn, preset, reset
  assign reg_out[8] = reg_out_en ? reg_int_out[8] : 1'bz;  // Controlled_Buffer controlled_buffer_2
  Multiplexer multiplexer_3 (.in0(reg_int_out[7]), .in1(reg_in[7]), .out(multiplexer_3_out), .sel(reg_in_en));
  D_Flip_Flop d_ff_3 (.D(multiplexer_3_out), .clk(reg_clk), .Q(reg_int_out[7]));  // open: Qn, preset, reset
  assign reg_out[7] = reg_out_en ? reg_int_out[7] : 1'bz;  // Controlled_Buffer controlled_buffer_3
  Multiplexer multiplexer_4 (.in0(reg_int_out[6]), .in1(reg_in[6]), .out(multiplexer_4_out), .sel(reg_in_en));
  D_Flip_Flop d_ff_4 (.D(multiplexer_4_out), .clk(reg_clk), .Q(reg_int_out[6]));  // open: Qn, preset, reset
  Multiplexer multiplexer_5 (.in0(reg_int_out[5]), .in1(reg_in[5]), .out(multiplexer_5_out), .sel(reg_in_en));
  assign reg_out[6] = reg_out_en ? reg_int_out[6] : 1'bz;  // Controlled_Buffer controlled_buffer_4
  Multiplexer multiplexer_6 (.in0(reg_int_out[4]), .in1(reg_in[4]), .out(multiplexer_6_out), .sel(reg_in_en));
  D_Flip_Flop d_ff_5 (.D(multiplexer_5_out), .clk(reg_clk), .Q(reg_int_out[5]));  // open: Qn, preset, reset
  Multiplexer multiplexer_7 (.in0(reg_int_out[3]), .in1(reg_in[3]), .out(multiplexer_7_out), .sel(reg_in_en));
  D_Flip_Flop d_ff_6 (.D(multiplexer_6_out), .clk(reg_clk), .Q(reg_int_out[4]));  // open: Qn, preset, reset
  assign reg_out[5] = reg_out_en ? reg_int_out[5] : 1'bz;  // Controlled_Buffer controlled_buffer_5
  assign reg_out[4] = reg_out_en ? reg_int_out[4] : 1'bz;  // Controlled_Buffer controlled_buffer_6
  Multiplexer multiplexer_8 (.in0(reg_int_out[2]), .in1(reg_in[2]), .out(multiplexer_8_out), .sel(reg_in_en));
  D_Flip_Flop d_ff_7 (.D(multiplexer_7_out), .clk(reg_clk), .Q(reg_int_out[3]));  // open: Qn, preset, reset
  Multiplexer multiplexer_9 (.in0(reg_int_out[1]), .in1(reg_in[1]), .out(multiplexer_9_out), .sel(reg_in_en));
  assign reg_out[3] = reg_out_en ? reg_int_out[3] : 1'bz;  // Controlled_Buffer controlled_buffer_7
  Multiplexer multiplexer_10 (.in0(reg_int_out[0]), .in1(reg_in[0]), .out(multiplexer_10_out), .sel(reg_in_en));
  D_Flip_Flop d_ff_8 (.D(multiplexer_8_out), .clk(reg_clk), .Q(reg_int_out[2]));  // open: Qn, preset, reset
  D_Flip_Flop d_ff_9 (.D(multiplexer_9_out), .clk(reg_clk), .Q(reg_int_out[1]));  // open: Qn, preset, reset
  assign reg_out[2] = reg_out_en ? reg_int_out[2] : 1'bz;  // Controlled_Buffer controlled_buffer_8
  assign reg_out[1] = reg_out_en ? reg_int_out[1] : 1'bz;  // Controlled_Buffer controlled_buffer_9
  D_Flip_Flop d_ff_10 (.D(multiplexer_10_out), .clk(reg_clk), .Q(reg_int_out[0]));  // open: Qn, preset, reset
  assign reg_out[0] = reg_out_en ? reg_int_out[0] : 1'bz;  // Controlled_Buffer controlled_buffer_10
endmodule

module alu (
  input  [9:0] alu_in_1,
  input  alu_out_en,
  input  alu_sub,
  input  [9:0] alu_in_2,
  output alu_zero_out,
  output alu_overflow_out,
  output alu_carry_out,
  output [9:0] alu_out,
  output alu_sign_out
);

  wire adder_2_cout, adder_3_cout, adder_4_cout, adder_5_cout, adder_6_cout, adder_7_cout, adder_8_cout,
       adder_9_cout, adder_10_cout, xor_2_out, xor_3_out, xor_4_out, xor_5_out, xor_6_out, xor_7_out,
       xor_8_out, xor_9_out, xor_10_out, xor_11_out;
  wire [8:0] adder_10_out;

  xor xor_1 (alu_overflow_out, adder_2_cout, alu_carry_out);
  Adder #(.width(1)) adder_1 (
    .a(alu_in_1[9]), .b(xor_2_out), .out(alu_sign_out), .cin(adder_2_cout), .cout(alu_carry_out));
  xor xor_2 (xor_2_out, alu_sub, alu_in_2[9]);
  Adder #(.width(1)) adder_2 (
    .a(alu_in_1[8]), .b(xor_3_out), .out(adder_10_out[8]), .cin(adder_3_cout), .cout(adder_2_cout));
  xor xor_3 (xor_3_out, alu_sub, alu_in_2[8]);
  Adder #(.width(1)) adder_3 (
    .a(alu_in_1[7]), .b(xor_4_out), .out(adder_10_out[7]), .cin(adder_4_cout), .cout(adder_3_cout));
  xor xor_4 (xor_4_out, alu_sub, alu_in_2[7]);
  Adder #(.width(1)) adder_4 (
    .a(alu_in_1[6]), .b(xor_5_out), .out(adder_10_out[6]), .cin(adder_5_cout), .cout(adder_4_cout));
  xor xor_5 (xor_5_out, alu_sub, alu_in_2[6]);
  Adder #(.width(1)) adder_5 (
    .a(alu_in_1[5]), .b(xor_6_out), .out(adder_10_out[5]), .cin(adder_6_cout), .cout(adder_5_cout));
  xor xor_6 (xor_6_out, alu_sub, alu_in_2[5]);
  Adder #(.width(1)) adder_6 (
    .a(alu_in_1[4]), .b(xor_7_out), .out(adder_10_out[4]), .cin(adder_7_cout), .cout(adder_6_cout));
  xor xor_7 (xor_7_out, alu_sub, alu_in_2[4]);
  Adder #(.width(1)) adder_7 (
    .a(alu_in_1[3]), .b(xor_8_out), .out(adder_10_out[3]), .cin(adder_8_cout), .cout(adder_7_cout));
  xor xor_8 (xor_8_out, alu_sub, alu_in_2[3]);
  xor xor_9 (xor_9_out, alu_sub, alu_in_2[2]);
  Adder #(.width(1)) adder_8 (
    .a(alu_in_1[2]), .b(xor_9_out), .out(adder_10_out[2]), .cin(adder_9_cout), .cout(adder_8_cout));
  Adder #(.width(1)) adder_9 (
    .a(alu_in_1[1]), .b(xor_10_out), .out(adder_10_out[1]), .cin(adder_10_cout), .cout(adder_9_cout));
  xor xor_10 (xor_10_out, alu_sub, alu_in_2[1]);
  xor xor_11 (xor_11_out, alu_sub, alu_in_2[0]);
  Adder #(.width(1)) adder_10 (
    .a(alu_in_1[0]), .b(xor_11_out), .out(adder_10_out[0]), .cin(alu_sub), .cout(adder_10_cout));
  nor nor_1 (alu_zero_out, adder_10_out[0], adder_10_out[1], adder_10_out[2], adder_10_out[3], adder_10_out[4], adder_10_out[5], adder_10_out[6], adder_10_out[7], adder_10_out[8], alu_sign_out);
  assign alu_out = alu_out_en ? {alu_sign_out, adder_10_out} : 10'bz;  // Controlled_Buffer controlled_buffer_1
endmodule

module pc (
  input  [5:0] pc_in,
  input  pc_en,
  input  pc_in_en,
  input  pc_clk,
  input  pc_reset,
  input  pc_out_en,
  output [5:0] pc_value,
  output [5:0] pc_out
);

  wire j_k_ff_2_qn, j_k_ff_3_qn, j_k_ff_4_qn, j_k_ff_5_qn, j_k_ff_6_qn, multiplexer_1_out, multiplexer_2_out,
       multiplexer_3_out, multiplexer_4_out, multiplexer_5_out, multiplexer_6_out, multiplexer_7_out,
       multiplexer_8_out, multiplexer_9_out, multiplexer_10_out, multiplexer_11_out, multiplexer_12_out,
       multiplexer_13_out, multiplexer_14_out, multiplexer_15_out, multiplexer_16_out, multiplexer_17_out,
       not_1_out, not_2_out, not_3_out, not_4_out, not_5_out, not_6_out;

  not not_1 (not_1_out, pc_in[5]);
  Multiplexer multiplexer_1 (.in0(pc_en), .in1(not_1_out), .out(multiplexer_1_out), .sel(pc_in_en));
  Multiplexer multiplexer_2 (.in0(pc_en), .in1(pc_in[5]), .out(multiplexer_2_out), .sel(pc_in_en));
  J_K_Flip_Flop j_k_ff_1 (
    .J(multiplexer_2_out), .K(multiplexer_1_out), .clk(multiplexer_3_out), .Q(pc_value[5]), .reset(pc_reset));  // open: Qn, preset
  Multiplexer multiplexer_3 (.in0(j_k_ff_2_qn), .in1(pc_clk), .out(multiplexer_3_out), .sel(pc_in_en));
  Multiplexer multiplexer_4 (.in0(pc_en), .in1(pc_in[4]), .out(multiplexer_4_out), .sel(pc_in_en));
  not not_2 (not_2_out, pc_in[4]);
  Multiplexer multiplexer_5 (.in0(pc_en), .in1(not_2_out), .out(multiplexer_5_out), .sel(pc_in_en));
  J_K_Flip_Flop j_k_ff_2 (
    .J(multiplexer_4_out), .K(multiplexer_5_out), .clk(multiplexer_7_out), .Q(pc_value[4]), .Qn(j_k_ff_2_qn),
    .reset(pc_reset));  // open: preset
  not not_3 (not_3_out, pc_in[3]);
  Multiplexer multiplexer_6 (.in0(pc_en), .in1(not_3_out), .out(multiplexer_6_out), .sel(pc_in_en));
  Multiplexer multiplexer_7 (.in0(j_k_ff_3_qn), .in1(pc_clk), .out(multiplexer_7_out), .sel(pc_in_en));
  Multiplexer multiplexer_8 (.in0(pc_en), .in1(pc_in[3]), .out(multiplexer_8_out), .sel(pc_in_en));
  J_K_Flip_Flop j_k_ff_3 (
    .J(multiplexer_8_out), .K(multiplexer_6_out), .clk(multiplexer_9_out), .Q(pc_value[3]), .Qn(j_k_ff_3_qn),
    .reset(pc_reset));  // open: preset
  Multiplexer multiplexer_9 (.in0(j_k_ff_4_qn), .in1(pc_clk), .out(multiplexer_9_out), .sel(pc_in_en));
  Multiplexer multiplexer_10 (.in0(pc_en), .in1(pc_in[2]), .out(multiplexer_10_out), .sel(pc_in_en));
  not not_4 (not_4_out, pc_in[2]);
  Multiplexer multiplexer_11 (.in0(pc_en), .in1(not_4_out), .out(multiplexer_11_out), .sel(pc_in_en));
  J_K_Flip_Flop j_k_ff_4 (
    .J(multiplexer_10_out), .K(multiplexer_11_out), .clk(multiplexer_13_out), .Q(pc_value[2]),
    .Qn(j_k_ff_4_qn), .reset(pc_reset));  // open: preset
  not not_5 (not_5_out, pc_in[1]);
  Multiplexer multiplexer_12 (.in0(pc_en), .in1(not_5_out), .out(multiplexer_12_out), .sel(pc_in_en));
  Multiplexer multiplexer_13 (.in0(j_k_ff_5_qn), .in1(pc_clk), .out(multiplexer_13_out), .sel(pc_in_en));
  Multiplexer multiplexer_14 (.in0(pc_en), .in1(pc_in[1]), .out(multiplexer_14_out), .sel(pc_in_en));
  J_K_Flip_Flop j_k_ff_5 (
    .J(multiplexer_14_out), .K(multiplexer_12_out), .clk(multiplexer_16_out), .Q(pc_value[1]),
    .Qn(j_k_ff_5_qn), .reset(pc_reset));  // open: preset
  not not_6 (not_6_out, pc_in[0]);
  Multiplexer multiplexer_15 (.in0(pc_en), .in1(not_6_out), .out(multiplexer_15_out), .sel(pc_in_en));
  Multiplexer multiplexer_16 (.in0(j_k_ff_6_qn), .in1(pc_clk), .out(multiplexer_16_out), .sel(pc_in_en));
  Multiplexer multiplexer_17 (.in0(pc_en), .in1(pc_in[0]), .out(multiplexer_17_out), .sel(pc_in_en));
  J_K_Flip_Flop j_k_ff_6 (
    .J(multiplexer_17_out), .K(multiplexer_15_out), .clk(pc_clk), .Q(pc_value[0]), .Qn(j_k_ff_6_qn),
    .reset(pc_reset));  // open: preset
  assign pc_out = pc_out_en ? pc_value : 6'bz;  // Controlled_Buffer controlled_buffer_1
endmodule

module dec_4x16 (
  input  [5:0] dec_sel,
  output [63:0] dec_out
);

  wire not_1_out, not_2_out, not_3_out, not_4_out, not_5_out, not_6_out;

  not not_1 (not_1_out, dec_sel[5]);
  not not_2 (not_2_out, dec_sel[4]);
  not not_3 (not_3_out, dec_sel[3]);
  not not_4 (not_4_out, dec_sel[2]);
  not not_5 (not_5_out, dec_sel[1]);
  not not_6 (not_6_out, dec_sel[0]);
  and and_1 (dec_out[0], not_2_out, not_6_out, not_5_out, not_4_out, not_3_out, not_1_out);
  and and_2 (dec_out[1], not_2_out, dec_sel[0], not_5_out, not_4_out, not_3_out, not_1_out);
  and and_3 (dec_out[2], not_2_out, not_6_out, dec_sel[1], not_4_out, not_3_out, not_1_out);
  and and_4 (dec_out[3], not_2_out, dec_sel[0], dec_sel[1], not_4_out, not_3_out, not_1_out);
  and and_5 (dec_out[4], not_2_out, not_6_out, not_5_out, dec_sel[2], not_3_out, not_1_out);
  and and_6 (dec_out[5], not_2_out, dec_sel[0], not_5_out, dec_sel[2], not_3_out, not_1_out);
  and and_7 (dec_out[6], not_2_out, not_6_out, dec_sel[1], dec_sel[2], not_3_out, not_1_out);
  and and_8 (dec_out[7], not_2_out, dec_sel[0], dec_sel[1], dec_sel[2], not_3_out, not_1_out);
  and and_9 (dec_out[8], not_2_out, not_6_out, not_5_out, not_4_out, dec_sel[3], not_1_out);
  and and_10 (dec_out[9], not_2_out, dec_sel[0], not_5_out, not_4_out, dec_sel[3], not_1_out);
  and and_11 (dec_out[10], not_2_out, not_6_out, dec_sel[1], not_4_out, dec_sel[3], not_1_out);
  and and_12 (dec_out[11], not_2_out, dec_sel[0], dec_sel[1], not_4_out, dec_sel[3], not_1_out);
  and and_13 (dec_out[12], not_2_out, not_6_out, not_5_out, dec_sel[2], dec_sel[3], not_1_out);
  and and_14 (dec_out[13], not_2_out, dec_sel[0], not_5_out, dec_sel[2], dec_sel[3], not_1_out);
  and and_15 (dec_out[14], not_2_out, not_6_out, dec_sel[1], dec_sel[2], dec_sel[3], not_1_out);
  and and_16 (dec_out[15], not_2_out, dec_sel[0], dec_sel[1], dec_sel[2], dec_sel[3], not_1_out);
  and and_17 (dec_out[16], dec_sel[4], not_6_out, not_5_out, not_4_out, not_3_out, not_1_out);
  and and_18 (dec_out[17], dec_sel[4], dec_sel[0], not_5_out, not_4_out, not_3_out, not_1_out);
  and and_19 (dec_out[18], dec_sel[4], not_6_out, dec_sel[1], not_4_out, not_3_out, not_1_out);
  and and_20 (dec_out[19], dec_sel[4], dec_sel[0], dec_sel[1], not_4_out, not_3_out, not_1_out);
  and and_21 (dec_out[20], dec_sel[4], not_6_out, not_5_out, dec_sel[2], not_3_out, not_1_out);
  and and_22 (dec_out[21], dec_sel[4], dec_sel[0], not_5_out, dec_sel[2], not_3_out, not_1_out);
  and and_23 (dec_out[22], dec_sel[4], not_6_out, dec_sel[1], dec_sel[2], not_3_out, not_1_out);
  and and_24 (dec_out[23], dec_sel[4], dec_sel[0], dec_sel[1], dec_sel[2], not_3_out, not_1_out);
  and and_25 (dec_out[24], dec_sel[4], not_6_out, not_5_out, not_4_out, dec_sel[3], not_1_out);
  and and_26 (dec_out[25], dec_sel[4], dec_sel[0], not_5_out, not_4_out, dec_sel[3], not_1_out);
  and and_27 (dec_out[26], dec_sel[4], not_6_out, dec_sel[1], not_4_out, dec_sel[3], not_1_out);
  and and_28 (dec_out[27], dec_sel[4], dec_sel[0], dec_sel[1], not_4_out, dec_sel[3], not_1_out);
  and and_29 (dec_out[28], dec_sel[4], not_6_out, not_5_out, dec_sel[2], dec_sel[3], not_1_out);
  and and_30 (dec_out[29], dec_sel[4], dec_sel[0], not_5_out, dec_sel[2], dec_sel[3], not_1_out);
  and and_31 (dec_out[30], dec_sel[4], not_6_out, dec_sel[1], dec_sel[2], dec_sel[3], not_1_out);
  and and_32 (dec_out[31], dec_sel[4], dec_sel[0], dec_sel[1], dec_sel[2], dec_sel[3], not_1_out);
  and and_33 (dec_out[32], not_2_out, not_6_out, not_5_out, not_4_out, not_3_out, dec_sel[5]);
  and and_34 (dec_out[33], not_2_out, dec_sel[0], not_5_out, not_4_out, not_3_out, dec_sel[5]);
  and and_35 (dec_out[34], not_2_out, not_6_out, dec_sel[1], not_4_out, not_3_out, dec_sel[5]);
  and and_36 (dec_out[35], not_2_out, dec_sel[0], dec_sel[1], not_4_out, not_3_out, dec_sel[5]);
  and and_37 (dec_out[36], not_2_out, not_6_out, not_5_out, dec_sel[2], not_3_out, dec_sel[5]);
  and and_38 (dec_out[37], not_2_out, dec_sel[0], not_5_out, dec_sel[2], not_3_out, dec_sel[5]);
  and and_39 (dec_out[38], not_2_out, not_6_out, dec_sel[1], dec_sel[2], not_3_out, dec_sel[5]);
  and and_40 (dec_out[39], not_2_out, dec_sel[0], dec_sel[1], dec_sel[2], not_3_out, dec_sel[5]);
  and and_41 (dec_out[40], not_2_out, not_6_out, not_5_out, not_4_out, dec_sel[3], dec_sel[5]);
  and and_42 (dec_out[41], not_2_out, dec_sel[0], not_5_out, not_4_out, dec_sel[3], dec_sel[5]);
  and and_43 (dec_out[42], not_2_out, not_6_out, dec_sel[1], not_4_out, dec_sel[3], dec_sel[5]);
  and and_44 (dec_out[43], not_2_out, dec_sel[0], dec_sel[1], not_4_out, dec_sel[3], dec_sel[5]);
  and and_45 (dec_out[44], not_2_out, not_6_out, not_5_out, dec_sel[2], dec_sel[3], dec_sel[5]);
  and and_46 (dec_out[45], not_2_out, dec_sel[0], not_5_out, dec_sel[2], dec_sel[3], dec_sel[5]);
  and and_47 (dec_out[46], not_2_out, not_6_out, dec_sel[1], dec_sel[2], dec_sel[3], dec_sel[5]);
  and and_48 (dec_out[47], not_2_out, dec_sel[0], dec_sel[1], dec_sel[2], dec_sel[3], dec_sel[5]);
  and and_49 (dec_out[48], dec_sel[4], not_6_out, not_5_out, not_4_out, not_3_out, dec_sel[5]);
  and and_50 (dec_out[49], dec_sel[4], dec_sel[0], not_5_out, not_4_out, not_3_out, dec_sel[5]);
  and and_51 (dec_out[50], dec_sel[4], not_6_out, dec_sel[1], not_4_out, not_3_out, dec_sel[5]);
  and and_52 (dec_out[51], dec_sel[4], dec_sel[0], dec_sel[1], not_4_out, not_3_out, dec_sel[5]);
  and and_53 (dec_out[52], dec_sel[4], not_6_out, not_5_out, dec_sel[2], not_3_out, dec_sel[5]);
  and and_54 (dec_out[53], dec_sel[4], dec_sel[0], not_5_out, dec_sel[2], not_3_out, dec_sel[5]);
  and and_55 (dec_out[54], dec_sel[4], not_6_out, dec_sel[1], dec_sel[2], not_3_out, dec_sel[5]);
  and and_56 (dec_out[55], dec_sel[4], dec_sel[0], dec_sel[1], dec_sel[2], not_3_out, dec_sel[5]);
  and and_57 (dec_out[56], dec_sel[4], not_6_out, not_5_out, not_4_out, dec_sel[3], dec_sel[5]);
  and and_58 (dec_out[57], dec_sel[4], dec_sel[0], not_5_out, not_4_out, dec_sel[3], dec_sel[5]);
  and and_59 (dec_out[58], dec_sel[4], not_6_out, dec_sel[1], not_4_out, dec_sel[3], dec_sel[5]);
  and and_60 (dec_out[59], dec_sel[4], dec_sel[0], dec_sel[1], not_4_out, dec_sel[3], dec_sel[5]);
  and and_61 (dec_out[60], dec_sel[4], not_6_out, not_5_out, dec_sel[2], dec_sel[3], dec_sel[5]);
  and and_62 (dec_out[61], dec_sel[4], dec_sel[0], not_5_out, dec_sel[2], dec_sel[3], dec_sel[5]);
  and and_63 (dec_out[62], dec_sel[4], not_6_out, dec_sel[1], dec_sel[2], dec_sel[3], dec_sel[5]);
  and and_64 (dec_out[63], dec_sel[4], dec_sel[0], dec_sel[1], dec_sel[2], dec_sel[3], dec_sel[5]);
endmodule

module sram_cell (
  input  [9:0] data_in,
  input  wr_en,
  input  clk,
  input  cs,
  input  rd_en,
  output [9:0] memory_content,
  output [9:0] data_out
);

  wire and_1_out, and_2_out;

  and and_1 (and_1_out, wr_en, cs);
  and and_2 (and_2_out, cs, rd_en);
  reg_gp reg_gp_1 (
    .reg_in(data_in), .reg_in_en(and_1_out), .reg_clk(clk), .reg_out_en(and_2_out),
    .reg_int_out(memory_content), .reg_out(data_out));
endmodule

module sram (
  input  [9:0] sram_d_in,
  input  sram_wr,
  input  sram_rd,
  input  [9:0] mar_d_in,
  input  mar_in_en,
  input  sram_clk,
  output [9:0] sram_d_out,
  output [9:0] out_8,
  output [9:0] out_9,
  output [9:0] out_10,
  output [9:0] out_11,
  output [9:0] out_12,
  output [9:0] out_13,
  output [9:0] out_14,
  output [9:0] out_15,
  output [9:0] out_16,
  output [9:0] out_17,
  output [9:0] out_18,
  output [9:0] out_19,
  output [9:0] out_20,
  output [9:0] out_21,
  output [9:0] out_22,
  output [9:0] out_23,
  output [9:0] out_24,
  output [9:0] out_25,
  output [9:0] out_26,
  output [9:0] out_27,
  output [9:0] out_28,
  output [9:0] out_29,
  output [9:0] out_30,
  output [9:0] out_31,
  output [9:0] out_32,
  output [9:0] out_33,
  output [9:0] out_34,
  output [9:0] out_35,
  output [9:0] out_36,
  output [9:0] out_37,
  output [9:0] out_38,
  output [9:0] out_39,
  output [9:0] out_40,
  output [9:0] out_41,
  output [9:0] out_42,
  output [9:0] out_43,
  output [9:0] out_44,
  output [9:0] out_45,
  output [9:0] out_46,
  output [9:0] out_47,
  output [9:0] out_48,
  output [9:0] out_49,
  output [9:0] out_50,
  output [9:0] out_51,
  output [9:0] out_52,
  output [9:0] out_53,
  output [9:0] out_54,
  output [9:0] out_55,
  output [9:0] out_56,
  output [9:0] out_57,
  output [9:0] out_58,
  output [9:0] out_59,
  output [9:0] out_60,
  output [9:0] out_61,
  output [9:0] out_62,
  output [9:0] out_63,
  output [9:0] out_64,
  output [9:0] out_65,
  output [9:0] out_66,
  output [9:0] out_67,
  output [9:0] out_68,
  output [9:0] out_69,
  output [9:0] out_70,
  output [9:0] out_71
);

  wire [9:0] controlled_buffer_1_out, reg_gp_1_reg_int_out;
  wire [63:0] dec_4x16_1_dec_out;

  reg_gp reg_gp_1 (
    .reg_in(mar_d_in), .reg_in_en(mar_in_en), .reg_clk(sram_clk), .reg_int_out(reg_gp_1_reg_int_out));  // open: reg_out_en, reg_out
  dec_4x16 dec_4x16_1 (.dec_sel(reg_gp_1_reg_int_out[5:0]), .dec_out(dec_4x16_1_dec_out));
  assign controlled_buffer_1_out = sram_wr ? sram_d_in : 10'bz;  // Controlled_Buffer controlled_buffer_1
  sram_cell sram_cell_1 (
    .data_in(controlled_buffer_1_out), .wr_en(sram_wr), .clk(sram_clk), .cs(dec_4x16_1_dec_out[0]),
    .rd_en(sram_rd), .memory_content(out_8), .data_out(controlled_buffer_1_out));
  sram_cell sram_cell_2 (
    .data_in(controlled_buffer_1_out), .wr_en(sram_wr), .clk(sram_clk), .cs(dec_4x16_1_dec_out[1]),
    .rd_en(sram_rd), .memory_content(out_9), .data_out(controlled_buffer_1_out));
  sram_cell sram_cell_3 (
    .data_in(controlled_buffer_1_out), .wr_en(sram_wr), .clk(sram_clk), .cs(dec_4x16_1_dec_out[2]),
    .rd_en(sram_rd), .memory_content(out_10), .data_out(controlled_buffer_1_out));
  sram_cell sram_cell_4 (
    .data_in(controlled_buffer_1_out), .wr_en(sram_wr), .clk(sram_clk), .cs(dec_4x16_1_dec_out[3]),
    .rd_en(sram_rd), .memory_content(out_11), .data_out(controlled_buffer_1_out));
  sram_cell sram_cell_5 (
    .data_in(controlled_buffer_1_out), .wr_en(sram_wr), .clk(sram_clk), .cs(dec_4x16_1_dec_out[4]),
    .rd_en(sram_rd), .memory_content(out_12), .data_out(controlled_buffer_1_out));
  sram_cell sram_cell_6 (
    .data_in(controlled_buffer_1_out), .wr_en(sram_wr), .clk(sram_clk), .cs(dec_4x16_1_dec_out[5]),
    .rd_en(sram_rd), .memory_content(out_13), .data_out(controlled_buffer_1_out));
  sram_cell sram_cell_7 (
    .data_in(controlled_buffer_1_out), .wr_en(sram_wr), .clk(sram_clk), .cs(dec_4x16_1_dec_out[6]),
    .rd_en(sram_rd), .memory_content(out_14), .data_out(controlled_buffer_1_out));
  sram_cell sram_cell_8 (
    .data_in(controlled_buffer_1_out), .wr_en(sram_wr), .clk(sram_clk), .cs(dec_4x16_1_dec_out[7]),
    .rd_en(sram_rd), .memory_content(out_15), .data_out(controlled_buffer_1_out));
  sram_cell sram_cell_9 (
    .data_in(controlled_buffer_1_out), .wr_en(sram_wr), .clk(sram_clk), .cs(dec_4x16_1_dec_out[8]),
    .rd_en(sram_rd), .memory_content(out_16), .data_out(controlled_buffer_1_out));
  sram_cell sram_cell_10 (
    .data_in(controlled_buffer_1_out), .wr_en(sram_wr), .clk(sram_clk), .cs(dec_4x16_1_dec_out[9]),
    .rd_en(sram_rd), .memory_content(out_17), .data_out(controlled_buffer_1_out));
  sram_cell sram_cell_11 (
    .data_in(controlled_buffer_1_out), .wr_en(sram_wr), .clk(sram_clk), .cs(dec_4x16_1_dec_out[10]),
    .rd_en(sram_rd), .memory_content(out_18), .data_out(controlled_buffer_1_out));
  sram_cell sram_cell_12 (
    .data_in(controlled_buffer_1_out), .wr_en(sram_wr), .clk(sram_clk), .cs(dec_4x16_1_dec_out[11]),
    .rd_en(sram_rd), .memory_content(out_19), .data_out(controlled_buffer_1_out));
  sram_cell sram_cell_13 (
    .data_in(controlled_buffer_1_out), .wr_en(sram_wr), .clk(sram_clk), .cs(dec_4x16_1_dec_out[12]),
    .rd_en(sram_rd), .memory_content(out_20), .data_out(controlled_buffer_1_out));
  sram_cell sram_cell_14 (
    .data_in(controlled_buffer_1_out), .wr_en(sram_wr), .clk(sram_clk), .cs(dec_4x16_1_dec_out[13]),
    .rd_en(sram_rd), .memory_content(out_21), .data_out(controlled_buffer_1_out));
  sram_cell sram_cell_15 (
    .data_in(controlled_buffer_1_out), .wr_en(sram_wr), .clk(sram_clk), .cs(dec_4x16_1_dec_out[14]),
    .rd_en(sram_rd), .memory_content(out_22), .data_out(controlled_buffer_1_out));
  sram_cell sram_cell_16 (
    .data_in(controlled_buffer_1_out), .wr_en(sram_wr), .clk(sram_clk), .cs(dec_4x16_1_dec_out[15]),
    .rd_en(sram_rd), .memory_content(out_23), .data_out(controlled_buffer_1_out));
  sram_cell sram_cell_17 (
    .data_in(controlled_buffer_1_out), .wr_en(sram_wr), .clk(sram_clk), .cs(dec_4x16_1_dec_out[16]),
    .rd_en(sram_rd), .memory_content(out_24), .data_out(controlled_buffer_1_out));
  sram_cell sram_cell_18 (
    .data_in(controlled_buffer_1_out), .wr_en(sram_wr), .clk(sram_clk), .cs(dec_4x16_1_dec_out[17]),
    .rd_en(sram_rd), .memory_content(out_25), .data_out(controlled_buffer_1_out));
  sram_cell sram_cell_19 (
    .data_in(controlled_buffer_1_out), .wr_en(sram_wr), .clk(sram_clk), .cs(dec_4x16_1_dec_out[18]),
    .rd_en(sram_rd), .memory_content(out_26), .data_out(controlled_buffer_1_out));
  sram_cell sram_cell_20 (
    .data_in(controlled_buffer_1_out), .wr_en(sram_wr), .clk(sram_clk), .cs(dec_4x16_1_dec_out[19]),
    .rd_en(sram_rd), .memory_content(out_27), .data_out(controlled_buffer_1_out));
  sram_cell sram_cell_21 (
    .data_in(controlled_buffer_1_out), .wr_en(sram_wr), .clk(sram_clk), .cs(dec_4x16_1_dec_out[20]),
    .rd_en(sram_rd), .memory_content(out_28), .data_out(controlled_buffer_1_out));
  sram_cell sram_cell_22 (
    .data_in(controlled_buffer_1_out), .wr_en(sram_wr), .clk(sram_clk), .cs(dec_4x16_1_dec_out[21]),
    .rd_en(sram_rd), .memory_content(out_29), .data_out(controlled_buffer_1_out));
  sram_cell sram_cell_23 (
    .data_in(controlled_buffer_1_out), .wr_en(sram_wr), .clk(sram_clk), .cs(dec_4x16_1_dec_out[22]),
    .rd_en(sram_rd), .memory_content(out_30), .data_out(controlled_buffer_1_out));
  sram_cell sram_cell_24 (
    .data_in(controlled_buffer_1_out), .wr_en(sram_wr), .clk(sram_clk), .cs(dec_4x16_1_dec_out[23]),
    .rd_en(sram_rd), .memory_content(out_31), .data_out(controlled_buffer_1_out));
  sram_cell sram_cell_25 (
    .data_in(controlled_buffer_1_out), .wr_en(sram_wr), .clk(sram_clk), .cs(dec_4x16_1_dec_out[24]),
    .rd_en(sram_rd), .memory_content(out_32), .data_out(controlled_buffer_1_out));
  sram_cell sram_cell_26 (
    .data_in(controlled_buffer_1_out), .wr_en(sram_wr), .clk(sram_clk), .cs(dec_4x16_1_dec_out[25]),
    .rd_en(sram_rd), .memory_content(out_33), .data_out(controlled_buffer_1_out));
  sram_cell sram_cell_27 (
    .data_in(controlled_buffer_1_out), .wr_en(sram_wr), .clk(sram_clk), .cs(dec_4x16_1_dec_out[26]),
    .rd_en(sram_rd), .memory_content(out_34), .data_out(controlled_buffer_1_out));
  sram_cell sram_cell_28 (
    .data_in(controlled_buffer_1_out), .wr_en(sram_wr), .clk(sram_clk), .cs(dec_4x16_1_dec_out[27]),
    .rd_en(sram_rd), .memory_content(out_35), .data_out(controlled_buffer_1_out));
  sram_cell sram_cell_29 (
    .data_in(controlled_buffer_1_out), .wr_en(sram_wr), .clk(sram_clk), .cs(dec_4x16_1_dec_out[28]),
    .rd_en(sram_rd), .memory_content(out_36), .data_out(controlled_buffer_1_out));
  sram_cell sram_cell_30 (
    .data_in(controlled_buffer_1_out), .wr_en(sram_wr), .clk(sram_clk), .cs(dec_4x16_1_dec_out[29]),
    .rd_en(sram_rd), .memory_content(out_37), .data_out(controlled_buffer_1_out));
  sram_cell sram_cell_31 (
    .data_in(controlled_buffer_1_out), .wr_en(sram_wr), .clk(sram_clk), .cs(dec_4x16_1_dec_out[30]),
    .rd_en(sram_rd), .memory_content(out_38), .data_out(controlled_buffer_1_out));
  sram_cell sram_cell_32 (
    .data_in(controlled_buffer_1_out), .wr_en(sram_wr), .clk(sram_clk), .cs(dec_4x16_1_dec_out[31]),
    .rd_en(sram_rd), .memory_content(out_39), .data_out(controlled_buffer_1_out));
  sram_cell sram_cell_33 (
    .data_in(controlled_buffer_1_out), .wr_en(sram_wr), .clk(sram_clk), .cs(dec_4x16_1_dec_out[32]),
    .rd_en(sram_rd), .memory_content(out_40), .data_out(controlled_buffer_1_out));
  sram_cell sram_cell_34 (
    .data_in(controlled_buffer_1_out), .wr_en(sram_wr), .clk(sram_clk), .cs(dec_4x16_1_dec_out[33]),
    .rd_en(sram_rd), .memory_content(out_41), .data_out(controlled_buffer_1_out));
  sram_cell sram_cell_35 (
    .data_in(controlled_buffer_1_out), .wr_en(sram_wr), .clk(sram_clk), .cs(dec_4x16_1_dec_out[34]),
    .rd_en(sram_rd), .memory_content(out_42), .data_out(controlled_buffer_1_out));
  sram_cell sram_cell_36 (
    .data_in(controlled_buffer_1_out), .wr_en(sram_wr), .clk(sram_clk), .cs(dec_4x16_1_dec_out[35]),
    .rd_en(sram_rd), .memory_content(out_43), .data_out(controlled_buffer_1_out));
  sram_cell sram_cell_37 (
    .data_in(controlled_buffer_1_out), .wr_en(sram_wr), .clk(sram_clk), .cs(dec_4x16_1_dec_out[36]),
    .rd_en(sram_rd), .memory_content(out_44), .data_out(controlled_buffer_1_out));
  sram_cell sram_cell_38 (
    .data_in(controlled_buffer_1_out), .wr_en(sram_wr), .clk(sram_clk), .cs(dec_4x16_1_dec_out[37]),
    .rd_en(sram_rd), .memory_content(out_45), .data_out(controlled_buffer_1_out));
  sram_cell sram_cell_39 (
    .data_in(controlled_buffer_1_out), .wr_en(sram_wr), .clk(sram_clk), .cs(dec_4x16_1_dec_out[38]),
    .rd_en(sram_rd), .memory_content(out_46), .data_out(controlled_buffer_1_out));
  sram_cell sram_cell_40 (
    .data_in(controlled_buffer_1_out), .wr_en(sram_wr), .clk(sram_clk), .cs(dec_4x16_1_dec_out[39]),
    .rd_en(sram_rd), .memory_content(out_47), .data_out(controlled_buffer_1_out));
  sram_cell sram_cell_41 (
    .data_in(controlled_buffer_1_out), .wr_en(sram_wr), .clk(sram_clk), .cs(dec_4x16_1_dec_out[40]),
    .rd_en(sram_rd), .memory_content(out_48), .data_out(controlled_buffer_1_out));
  sram_cell sram_cell_42 (
    .data_in(controlled_buffer_1_out), .wr_en(sram_wr), .clk(sram_clk), .cs(dec_4x16_1_dec_out[41]),
    .rd_en(sram_rd), .memory_content(out_49), .data_out(controlled_buffer_1_out));
  sram_cell sram_cell_43 (
    .data_in(controlled_buffer_1_out), .wr_en(sram_wr), .clk(sram_clk), .cs(dec_4x16_1_dec_out[42]),
    .rd_en(sram_rd), .memory_content(out_50), .data_out(controlled_buffer_1_out));
  sram_cell sram_cell_44 (
    .data_in(controlled_buffer_1_out), .wr_en(sram_wr), .clk(sram_clk), .cs(dec_4x16_1_dec_out[43]),
    .rd_en(sram_rd), .memory_content(out_51), .data_out(controlled_buffer_1_out));
  sram_cell sram_cell_45 (
    .data_in(controlled_buffer_1_out), .wr_en(sram_wr), .clk(sram_clk), .cs(dec_4x16_1_dec_out[44]),
    .rd_en(sram_rd), .memory_content(out_52), .data_out(controlled_buffer_1_out));
  sram_cell sram_cell_46 (
    .data_in(controlled_buffer_1_out), .wr_en(sram_wr), .clk(sram_clk), .cs(dec_4x16_1_dec_out[45]),
    .rd_en(sram_rd), .memory_content(out_53), .data_out(controlled_buffer_1_out));
  sram_cell sram_cell_47 (
    .data_in(controlled_buffer_1_out), .wr_en(sram_wr), .clk(sram_clk), .cs(dec_4x16_1_dec_out[46]),
    .rd_en(sram_rd), .memory_content(out_54), .data_out(controlled_buffer_1_out));
  sram_cell sram_cell_48 (
    .data_in(controlled_buffer_1_out), .wr_en(sram_wr), .clk(sram_clk), .cs(dec_4x16_1_dec_out[47]),
    .rd_en(sram_rd), .memory_content(out_55), .data_out(controlled_buffer_1_out));
  sram_cell sram_cell_49 (
    .data_in(controlled_buffer_1_out), .wr_en(sram_wr), .clk(sram_clk), .cs(dec_4x16_1_dec_out[48]),
    .rd_en(sram_rd), .memory_content(out_56), .data_out(controlled_buffer_1_out));
  sram_cell sram_cell_50 (
    .data_in(controlled_buffer_1_out), .wr_en(sram_wr), .clk(sram_clk), .cs(dec_4x16_1_dec_out[49]),
    .rd_en(sram_rd), .memory_content(out_57), .data_out(controlled_buffer_1_out));
  sram_cell sram_cell_51 (
    .data_in(controlled_buffer_1_out), .wr_en(sram_wr), .clk(sram_clk), .cs(dec_4x16_1_dec_out[50]),
    .rd_en(sram_rd), .memory_content(out_58), .data_out(controlled_buffer_1_out));
  sram_cell sram_cell_52 (
    .data_in(controlled_buffer_1_out), .wr_en(sram_wr), .clk(sram_clk), .cs(dec_4x16_1_dec_out[51]),
    .rd_en(sram_rd), .memory_content(out_59), .data_out(controlled_buffer_1_out));
  sram_cell sram_cell_53 (
    .data_in(controlled_buffer_1_out), .wr_en(sram_wr), .clk(sram_clk), .cs(dec_4x16_1_dec_out[52]),
    .rd_en(sram_rd), .memory_content(out_60), .data_out(controlled_buffer_1_out));
  sram_cell sram_cell_54 (
    .data_in(controlled_buffer_1_out), .wr_en(sram_wr), .clk(sram_clk), .cs(dec_4x16_1_dec_out[53]),
    .rd_en(sram_rd), .memory_content(out_61), .data_out(controlled_buffer_1_out));
  sram_cell sram_cell_55 (
    .data_in(controlled_buffer_1_out), .wr_en(sram_wr), .clk(sram_clk), .cs(dec_4x16_1_dec_out[54]),
    .rd_en(sram_rd), .memory_content(out_62), .data_out(controlled_buffer_1_out));
  sram_cell sram_cell_56 (
    .data_in(controlled_buffer_1_out), .wr_en(sram_wr), .clk(sram_clk), .cs(dec_4x16_1_dec_out[55]),
    .rd_en(sram_rd), .memory_content(out_63), .data_out(controlled_buffer_1_out));
  sram_cell sram_cell_57 (
    .data_in(controlled_buffer_1_out), .wr_en(sram_wr), .clk(sram_clk), .cs(dec_4x16_1_dec_out[56]),
    .rd_en(sram_rd), .memory_content(out_64), .data_out(controlled_buffer_1_out));
  sram_cell sram_cell_58 (
    .data_in(controlled_buffer_1_out), .wr_en(sram_wr), .clk(sram_clk), .cs(dec_4x16_1_dec_out[57]),
    .rd_en(sram_rd), .memory_content(out_65), .data_out(controlled_buffer_1_out));
  sram_cell sram_cell_59 (
    .data_in(controlled_buffer_1_out), .wr_en(sram_wr), .clk(sram_clk), .cs(dec_4x16_1_dec_out[58]),
    .rd_en(sram_rd), .memory_content(out_66), .data_out(controlled_buffer_1_out));
  sram_cell sram_cell_60 (
    .data_in(controlled_buffer_1_out), .wr_en(sram_wr), .clk(sram_clk), .cs(dec_4x16_1_dec_out[59]),
    .rd_en(sram_rd), .memory_content(out_67), .data_out(controlled_buffer_1_out));
  sram_cell sram_cell_61 (
    .data_in(controlled_buffer_1_out), .wr_en(sram_wr), .clk(sram_clk), .cs(dec_4x16_1_dec_out[60]),
    .rd_en(sram_rd), .memory_content(out_68), .data_out(controlled_buffer_1_out));
  sram_cell sram_cell_62 (
    .data_in(controlled_buffer_1_out), .wr_en(sram_wr), .clk(sram_clk), .cs(dec_4x16_1_dec_out[61]),
    .rd_en(sram_rd), .memory_content(out_69), .data_out(controlled_buffer_1_out));
  sram_cell sram_cell_63 (
    .data_in(controlled_buffer_1_out), .wr_en(sram_wr), .clk(sram_clk), .cs(dec_4x16_1_dec_out[62]),
    .rd_en(sram_rd), .memory_content(out_70), .data_out(controlled_buffer_1_out));
  sram_cell sram_cell_64 (
    .data_in(controlled_buffer_1_out), .wr_en(sram_wr), .clk(sram_clk), .cs(dec_4x16_1_dec_out[63]),
    .rd_en(sram_rd), .memory_content(out_71), .data_out(controlled_buffer_1_out));
  assign sram_d_out = sram_rd ? controlled_buffer_1_out : 10'bz;  // Controlled_Buffer controlled_buffer_2
endmodule

module ins_reg (
  input  [9:0] ins_reg_in,
  input  ins_reg_in_en,
  input  clk,
  input  ins_reg_out_en,
  output [9:0] out_5,
  output [5:0] add_outs,
  output [3:0] ins_out
);

  reg_gp reg_gp_1 (
    .reg_in(ins_reg_in), .reg_in_en(ins_reg_in_en), .reg_clk(clk), .reg_int_out({ins_out, out_5[5:0]}));  // open: reg_out_en, reg_out
  assign add_outs = ins_reg_out_en ? out_5[5:0] : 6'bz;  // Controlled_Buffer controlled_buffer_1

  assign out_5[9:6] = ins_out;
endmodule

module cs (
  input  debug,
  input  clk,
  input  ring_reset,
  input  [3:0] data_in,
  input  [9:0] flag_reg,
  output pc_en,
  output pc_out,
  output pc_reset,
  output sram_wr,
  output [5:0] out_10,
  output sram_rd,
  output mar_in_en,
  output ins_reg_in_en,
  output ins_reg_out_en,
  output a_in,
  output a_out,
  output alu_out,
  output alu_sub,
  output b_in,
  output b_out,
  output ram_rd,
  output pc_in_en,
  output flag_clk,
  output amount_in,
  output shift_in,
  output shift_out,
  output rotate_in,
  output rotate_out
);

  wire and_1_out, and_2_out, and_3_out, and_4_out, and_5_out, and_6_out, and_7_out, and_8_out, and_9_out,
       and_10_out, and_11_out, and_12_out, and_13_out, and_14_out, and_15_out, and_16_out, and_17_out,
       and_18_out, and_19_out, and_20_out, and_21_out, and_22_out, and_23_out, and_24_out, and_25_out,
       and_26_out, and_27_out, and_28_out, and_29_out, and_30_out, and_31_out, and_32_out, and_33_out,
       and_34_out, and_35_out, and_36_out, and_37_out, and_38_out, and_39_out, and_40_out, and_41_out,
       and_42_out, and_43_out, and_44_out, and_45_out, and_46_out, and_47_out, and_48_out, and_49_out,
       and_50_out, and_51_out, and_52_out, and_53_out, and_54_out, and_55_out, and_56_out, and_57_out,
       and_58_out, and_59_out, and_60_out, and_61_out, and_66_out, controlled_buffer_1_out,
       demultiplexer_1_out0, nor_1_out, not_1_out, not_2_out, not_3_out, not_4_out, not_5_out, not_6_out,
       not_7_out, not_8_out, ring_reset_t, sram_wr_tunnel;
  wire [3:0] multiplexer_1_out, pull_resistor_1_node;
  wire [5:5] pull_resistor_2_node;
  wire [7:0] ring_counter_1_ring_out;
  wire [63:0] dec_4x16_1_dec_out;

  Pull_Resistor pull_resistor_1 (.node(pull_resistor_1_node));
  Multiplexer #(.width(4)) multiplexer_1 (
    .in0(pull_resistor_1_node), .in1(data_in), .out(multiplexer_1_out), .sel(not_1_out));
  not not_1 (not_1_out, debug);
  Pull_Resistor pull_resistor_2 (.node(pull_resistor_2_node[5]));
  assign controlled_buffer_1_out = ring_reset ? ring_reset : 1'bz;  // Controlled_Buffer controlled_buffer_1
  assign controlled_buffer_1_out = not_2_out ? ring_reset_t : 1'bz;  // Controlled_Buffer controlled_buffer_2
  not not_2 (not_2_out, ring_reset);
  dec_4x16 dec_4x16_1 (.dec_sel({{2{pull_resistor_2_node[5]}}, multiplexer_1_out}), .dec_out(dec_4x16_1_dec_out));
  ring_counter ring_counter_1 (
    .clk(clk), .ring_reset(controlled_buffer_1_out), .ring_value(out_10), .ring_out(ring_counter_1_ring_out));
  not not_3 (not_3_out, flag_reg[0]);
  not not_4 (not_4_out, flag_reg[2]);
  not not_5 (not_5_out, flag_reg[0]);
  not not_6 (not_6_out, flag_reg[2]);
  not not_7 (not_7_out, flag_reg[0]);
  not not_8 (not_8_out, flag_reg[2]);
  and and_1 (and_1_out, dec_4x16_1_dec_out[1], ring_counter_1_ring_out[2]);
  and and_2 (and_2_out, dec_4x16_1_dec_out[2], ring_counter_1_ring_out[2]);
  and and_3 (and_3_out, ring_counter_1_ring_out[2], dec_4x16_1_dec_out[3]);
  and and_4 (and_4_out, ring_counter_1_ring_out[2], dec_4x16_1_dec_out[4]);
  and and_5 (and_5_out, ring_counter_1_ring_out[3], dec_4x16_1_dec_out[6]);
  and and_6 (and_6_out, ring_counter_1_ring_out[2], dec_4x16_1_dec_out[7]);
  and and_7 (and_7_out, ring_counter_1_ring_out[2], dec_4x16_1_dec_out[8]);
  and and_8 (and_8_out, dec_4x16_1_dec_out[1], ring_counter_1_ring_out[3]);
  and and_9 (and_9_out, dec_4x16_1_dec_out[2], ring_counter_1_ring_out[3]);
  and and_10 (and_10_out, dec_4x16_1_dec_out[6], ring_counter_1_ring_out[4]);
  and and_11 (and_11_out, dec_4x16_1_dec_out[8], ring_counter_1_ring_out[3]);
  and and_12 (and_12_out, dec_4x16_1_dec_out[10], not_3_out);
  and and_13 (and_13_out, dec_4x16_1_dec_out[11], not_4_out);
  and and_14 (and_14_out, dec_4x16_1_dec_out[1], ring_counter_1_ring_out[2]);
  and and_15 (and_15_out, dec_4x16_1_dec_out[2], ring_counter_1_ring_out[2]);
  and and_16 (and_16_out, dec_4x16_1_dec_out[3], ring_counter_1_ring_out[2]);
  and and_17 (and_17_out, dec_4x16_1_dec_out[4], ring_counter_1_ring_out[2]);
  and and_18 (and_18_out, dec_4x16_1_dec_out[7], ring_counter_1_ring_out[2]);
  and and_19 (and_19_out, ring_counter_1_ring_out[2], dec_4x16_1_dec_out[8]);
  and and_20 (and_20_out, ring_counter_1_ring_out[2], dec_4x16_1_dec_out[9]);
  and and_21 (and_21_out, ring_counter_1_ring_out[2], not_5_out, dec_4x16_1_dec_out[10]);
  and and_22 (and_22_out, ring_counter_1_ring_out[2], not_6_out, dec_4x16_1_dec_out[11]);
  and and_23 (and_23_out, ring_counter_1_ring_out[2], dec_4x16_1_dec_out[12]);
  and and_24 (and_24_out, ring_counter_1_ring_out[2], dec_4x16_1_dec_out[13]);
  and and_25 (and_25_out, dec_4x16_1_dec_out[1], ring_counter_1_ring_out[3]);
  and and_26 (and_26_out, ring_counter_1_ring_out[4], dec_4x16_1_dec_out[6]);
  and and_27 (and_27_out, ring_counter_1_ring_out[4], dec_4x16_1_dec_out[12]);
  and and_28 (and_28_out, ring_counter_1_ring_out[4], dec_4x16_1_dec_out[13]);
  and and_29 (and_29_out, dec_4x16_1_dec_out[1], ring_counter_1_ring_out[4]);
  and and_30 (and_30_out, dec_4x16_1_dec_out[2], ring_counter_1_ring_out[4]);
  and and_31 (and_31_out, ring_counter_1_ring_out[4], dec_4x16_1_dec_out[3]);
  and and_32 (and_32_out, dec_4x16_1_dec_out[4], ring_counter_1_ring_out[4]);
  and and_33 (and_33_out, ring_counter_1_ring_out[2], dec_4x16_1_dec_out[5]);
  and and_34 (and_34_out, dec_4x16_1_dec_out[0], ring_counter_1_ring_out[3]);
  and and_35 (and_35_out, ring_counter_1_ring_out[5], dec_4x16_1_dec_out[6]);
  and and_36 (and_36_out, dec_4x16_1_dec_out[7], ring_counter_1_ring_out[4]);
  and and_37 (and_37_out, ring_counter_1_ring_out[5], dec_4x16_1_dec_out[8]);
  and and_38 (and_38_out, ring_counter_1_ring_out[3], dec_4x16_1_dec_out[9]);
  and and_39 (and_39_out, ring_counter_1_ring_out[3], dec_4x16_1_dec_out[10]);
  and and_40 (and_40_out, ring_counter_1_ring_out[3], dec_4x16_1_dec_out[11]);
  and and_41 (and_41_out, ring_counter_1_ring_out[5], dec_4x16_1_dec_out[12]);
  and and_42 (and_42_out, ring_counter_1_ring_out[5], dec_4x16_1_dec_out[13]);
  and and_43 (and_43_out, dec_4x16_1_dec_out[2], ring_counter_1_ring_out[3]);
  and and_44 (and_44_out, dec_4x16_1_dec_out[8], ring_counter_1_ring_out[3]);
  and and_45 (and_45_out, dec_4x16_1_dec_out[3], ring_counter_1_ring_out[3]);
  and and_46 (and_46_out, dec_4x16_1_dec_out[4], ring_counter_1_ring_out[3]);
  and and_47 (and_47_out, dec_4x16_1_dec_out[7], ring_counter_1_ring_out[3]);
  and and_48 (and_48_out, dec_4x16_1_dec_out[3], ring_counter_1_ring_out[3]);
  and and_49 (and_49_out, dec_4x16_1_dec_out[4], ring_counter_1_ring_out[3]);
  and and_50 (and_50_out, dec_4x16_1_dec_out[4], ring_counter_1_ring_out[3]);
  and and_51 (and_51_out, ring_counter_1_ring_out[4], dec_4x16_1_dec_out[8]);
  and and_52 (and_52_out, ring_counter_1_ring_out[5], dec_4x16_1_dec_out[8]);
  and and_53 (and_53_out, dec_4x16_1_dec_out[7], ring_counter_1_ring_out[3]);
  and and_54 (and_54_out, dec_4x16_1_dec_out[12], ring_counter_1_ring_out[3]);
  and and_55 (and_55_out, dec_4x16_1_dec_out[13], ring_counter_1_ring_out[3]);
  and and_56 (and_56_out, dec_4x16_1_dec_out[8], ring_counter_1_ring_out[5]);
  and and_57 (and_57_out, dec_4x16_1_dec_out[9], ring_counter_1_ring_out[2]);
  and and_58 (and_58_out, dec_4x16_1_dec_out[10], not_7_out, ring_counter_1_ring_out[2]);
  and and_59 (and_59_out, dec_4x16_1_dec_out[11], not_8_out, ring_counter_1_ring_out[2]);
  and and_60 (and_60_out, dec_4x16_1_dec_out[12], ring_counter_1_ring_out[2]);
  and and_61 (and_61_out, dec_4x16_1_dec_out[13], ring_counter_1_ring_out[2]);
  and and_62 (shift_in, dec_4x16_1_dec_out[12], ring_counter_1_ring_out[3]);
  and and_63 (shift_out, dec_4x16_1_dec_out[12], ring_counter_1_ring_out[4]);
  and and_64 (rotate_in, ring_counter_1_ring_out[3], dec_4x16_1_dec_out[13]);
  and and_65 (rotate_out, ring_counter_1_ring_out[4], dec_4x16_1_dec_out[13]);
  and and_66 (and_66_out, dec_4x16_1_dec_out[6], ring_counter_1_ring_out[3]);
  Demultiplexer demultiplexer_1 (
    .out0(demultiplexer_1_out0), .out1(ram_rd), .in(ring_counter_1_ring_out[1]), .sel(debug));
  Demultiplexer demultiplexer_2 (
    .out0(ins_reg_in_en), .out1(sram_wr_tunnel), .in(ring_counter_1_ring_out[1]), .sel(debug));
  nor nor_1 (nor_1_out, dec_4x16_1_dec_out[5], dec_4x16_1_dec_out[9], and_12_out, and_13_out);
  or or_1 (a_in, and_25_out, and_26_out, and_27_out, and_28_out);
  or or_2 (a_out, and_53_out, and_54_out, and_55_out);
  or or_3 (pc_out, ring_counter_1_ring_out[0], and_66_out);
  and and_67 (pc_en, ring_counter_1_ring_out[2], nor_1_out);
  or or_4 (ins_reg_out_en, and_21_out, and_19_out, and_14_out, and_16_out, and_18_out, and_17_out, and_15_out, and_20_out, and_22_out, and_23_out, and_24_out);
  or or_5 (ring_reset_t, and_37_out, and_29_out, and_36_out, and_31_out, and_33_out, and_38_out, and_32_out, and_30_out, and_34_out, and_35_out, and_39_out, and_40_out, and_41_out, and_42_out);
  or or_6 (b_in, and_43_out, and_44_out);
  or or_7 (sram_wr, and_45_out, and_47_out, sram_wr_tunnel, and_46_out);
  or or_8 (alu_out, and_48_out, and_49_out);
  or or_9 (alu_sub, and_50_out, and_52_out, and_51_out);
  buf or_10 (flag_clk, and_56_out);  // OR_Gate
  or or_11 (pc_in_en, and_57_out, and_59_out, and_58_out);
  or or_12 (amount_in, and_60_out, and_61_out);
  or or_13 (mar_in_en, and_4_out, and_5_out, ring_counter_1_ring_out[0], and_2_out, and_3_out, and_1_out, and_6_out, and_7_out);
  or or_14 (sram_rd, demultiplexer_1_out0, and_9_out, and_10_out, and_11_out, and_8_out);
  Pull_Resistor pull_resistor_3 (.node(b_out));

  // Notes on the sheet:
  //   S C O Z
  //   1. LDA
  //   2. LDB
  //   3. OUT
  //   4. SUB
  //   5. HLT
  //   6. LDI
  //   7. STA
  //   8. CMP
  //   9. JMP
  //   10. JNZ
  //   11. JNC
  //   12.SFT
  //   13.RTE
  //   0. Debug
endmodule

module ring_counter (
  input  clk,
  input  ring_reset,
  output [5:0] ring_value,
  output [7:0] ring_out
);

  wire controlled_buffer_1_out, not_1_out, pull_resistor_1_node, pull_resistor_3_node;
  wire [5:0] pc_new_1_pc_out, pull_resistor_2_node;
  wire [63:8] dec_4x16_1_dec_out;

  assign controlled_buffer_1_out = ring_reset ? ring_reset : 1'bz;  // Controlled_Buffer controlled_buffer_1
  not not_1 (not_1_out, ring_reset);
  Pull_Resistor pull_resistor_1 (.node(pull_resistor_1_node));
  Pull_Resistor pull_resistor_2 (.node(pull_resistor_2_node));
  Pull_Resistor #(.pull(1)) pull_resistor_3 (.node(pull_resistor_3_node));
  assign controlled_buffer_1_out = not_1_out ? ring_out[7] : 1'bz;  // Controlled_Buffer controlled_buffer_2
  pc_new pc_new_1 (
    .pc_en(pull_resistor_3_node), .pc_in(pull_resistor_2_node), .pc_in_en(pull_resistor_1_node),
    .pc_reset(controlled_buffer_1_out), .pc_clk(clk), .pc_out_en(pull_resistor_3_node),
    .pc_value(ring_value), .pc_out(pc_new_1_pc_out));
  dec_4x16 dec_4x16_1 (.dec_sel(pc_new_1_pc_out), .dec_out({dec_4x16_1_dec_out, ring_out}));
endmodule

module copy (
  input  in_1,
  input  in_2,
  input  in_3,
  input  in_4,
  input  in_5,
  input  in_6,
  input  in_7,
  input  in_8,
  input  in_9,
  input  in_10,
  input  in_11,
  input  in_12,
  input  in_13,
  input  in_14,
  input  [7:0] in_15,
  input  in_16,
  input  in_17,
  output [7:0] out_18,
  output [3:0] out_19,
  output out_20,
  output [7:0] out_21,
  output [7:0] reg_0,
  output [7:0] reg_1,
  output [7:0] reg_2,
  output [7:0] reg_3,
  output [7:0] reg_4,
  output [7:0] reg_5,
  output [7:0] reg_6,
  output [7:0] reg_7,
  output [7:0] reg_8,
  output [7:0] reg_9,
  output [3:0] out_32,
  output [7:0] reg_10,
  output [3:0] out_34,
  output [7:0] reg_11,
  output [7:0] reg_12,
  output [3:0] out_37,
  output [7:0] reg_13,
  output [7:0] reg_14,
  output [7:0] reg_15,
  output [7:0] out_41
);

  // pc pc_1: pin names not known; wires that end beside it: in_9, in_7, in_11, in_13, out_19, out_32
  // sram sram_1: pin names not known; wires that end beside it: {out_41[7:4], out_32}, in_1, in_3, {out_41[7:4], out_32}, in_5, in_7, {out_41[7:4], out_32}, reg_0, reg_1, reg_2, reg_3, reg_4, reg_5, reg_6, reg_7, reg_8, reg_9, reg_10, reg_11, reg_12, reg_13, reg_14, reg_15
  assign {out_41[7:4], out_32} = in_17 ? in_15 : 8'bz;  // Controlled_Buffer controlled_buffer_1
  // reg_gp reg_gp_1: pin names not known; wires that end beside it: {out_41[7:4], out_32}, in_6, in_7, in_8, out_18, {out_41[7:4], out_32}
  // reg_gp reg_gp_2: pin names not known; wires that end beside it: {out_41[7:4], out_32}, in_10, in_7, in_12, out_21, {out_41[7:4], out_32}
  // ins_reg ins_reg_1: pin names not known; wires that end beside it: {out_41[7:4], out_32}, in_2, in_7, in_4, out_32, out_34
  // alu alu_1: pin names not known; wires that end beside it: out_18, in_14, in_16, out_21, out_20, {out_41[7:4], out_32}
  // cs cs_1: pin names not known; wires that end beside it: in_7, out_34, in_9, in_13, in_11, out_37, in_1, in_3, in_5, in_2, in_4, in_6, in_8, in_14, in_16, in_10, in_12

  assign out_41[3:0] = out_32;

  // Other names for the same wires on the sheet: a_in = in_6; a_out = in_8; alu_out = in_14; alu_sub = in_16;
  //   b_in = in_10; b_out = in_12; clk = in_7; debug = in_17; debug_data[7:0] = in_15; ins_reg_in_en = in_2;
  //   ins_reg_out_en = in_4; mar_in_en = in_5; pc_en = in_9; pc_out = in_13; pc_reset = in_11; sram_rd = in_3;
  //   sram_wr = in_1

  // Notes on the sheet:
  //   Clock
  //   RAM control
  //   PC control
  //   Debug & Testing
  //   IR control
  //   Register A control
  //   Register B control
  //   ALU control
endmodule

module copy2 (
  input  in_1,
  input  in_2,
  input  [7:0] in_3,
  input  in_4,
  input  in_5,
  input  in_6,
  input  [7:0] in_7,
  input  in_8,
  output [7:0] out_9,
  output [3:0] out_10,
  output out_11,
  output [3:0] out_12,
  output [7:0] out_13,
  output [7:0] out_14,
  output [7:0] out_15,
  output [3:0] out_16,
  output [3:0] out_17,
  output [3:0] out_18,
  output [7:0] out_19
);

  wire a_in, a_out, alu_out, alu_sub, b_in, b_out, clk, ins_reg_in_en, ins_reg_out_en, mar_in_en, pc_en,
       pc_out, sram_rd, sram_wr;
  wire [7:0] ram_1_dout;
  wire [7:4] reg_gp_1_p4;

  // reg_gp reg_gp_1: pin names not known; wires that end beside it: out_14, mar_in_en, clk, {reg_gp_1_p4, out_12}
  RAM #(.addrWidth(4), .trigger("falling")) ram_1 (
    .addr(out_12), .we(sram_wr), .oe(sram_rd), .clk(clk), .din(out_14), .dout(ram_1_dout));
  // pc pc_1: pin names not known; wires that end beside it: pc_en, clk, in_1, pc_out, out_10, out_14[3:0]
  assign out_14 = sram_rd ? ram_1_dout : 8'bz;  // Controlled_Buffer controlled_buffer_1
  assign out_14 = in_4 ? in_3 : 8'bz;  // Controlled_Buffer controlled_buffer_2
  Clock clock_1 (.out(clk));
  // reg_gp reg_gp_2: pin names not known; wires that end beside it: out_14, a_in, clk, a_out, out_9, out_14
  // reg_gp reg_gp_3: pin names not known; wires that end beside it: out_14, b_in, clk, b_out, out_13, out_14
  // ins_reg ins_reg_1: pin names not known; wires that end beside it: out_14, ins_reg_in_en, clk, ins_reg_out_en, out_15, out_14[3:0], out_17
  // alu alu_1: pin names not known; wires that end beside it: out_9, alu_out, alu_sub, out_13, out_11, out_14
  // cs cs_1: pin names not known; wires that end beside it: clk, in_2, out_17, pc_en, pc_out, in_1, sram_wr, out_18, sram_rd, mar_in_en, ins_reg_in_en, ins_reg_out_en, a_in, a_out, alu_out, alu_sub, b_in, b_out

  assign out_16 = out_14[3:0];
  assign out_19 = out_14;

  // Other names for the same wires on the sheet: debug = in_4; debug_data[7:0] = in_3; pc_reset = in_1;
  //   ring_reset = in_2

  // Notes on the sheet:
  //   Clock
  //   Debug & Testing
endmodule

module pc_new (
  input  pc_en,
  input  [5:0] pc_in,
  input  pc_in_en,
  input  pc_reset,
  input  pc_clk,
  input  pc_out_en,
  output [5:0] pc_value,
  output [5:0] pc_out
);

  wire and_1_out, and_2_out, and_3_out, and_4_out, and_5_out, multiplexer_1_out, multiplexer_2_out,
       multiplexer_3_out, multiplexer_4_out, multiplexer_5_out, multiplexer_6_out, multiplexer_7_out,
       multiplexer_8_out, multiplexer_9_out, multiplexer_10_out, multiplexer_11_out, multiplexer_12_out,
       not_1_out, not_2_out, not_3_out, not_4_out, not_5_out, not_6_out;

  Multiplexer multiplexer_1 (.in0(and_1_out), .in1(not_1_out), .out(multiplexer_1_out), .sel(pc_in_en));
  and and_1 (and_1_out, pc_en, pc_value[4], pc_value[3], pc_value[2], pc_value[1], pc_value[0]);
  not not_1 (not_1_out, pc_in[5]);
  Multiplexer multiplexer_2 (.in0(and_1_out), .in1(pc_in[5]), .out(multiplexer_2_out), .sel(pc_in_en));
  J_K_Flip_Flop j_k_ff_1 (
    .J(multiplexer_2_out), .K(multiplexer_1_out), .clk(pc_clk), .Q(pc_value[5]), .reset(pc_reset));  // open: Qn, preset
  and and_2 (and_2_out, pc_en, pc_value[3], pc_value[2], pc_value[1], pc_value[0]);
  Multiplexer multiplexer_3 (.in0(and_2_out), .in1(pc_in[4]), .out(multiplexer_3_out), .sel(pc_in_en));
  Multiplexer multiplexer_4 (.in0(and_2_out), .in1(not_2_out), .out(multiplexer_4_out), .sel(pc_in_en));
  J_K_Flip_Flop j_k_ff_2 (
    .J(multiplexer_3_out), .K(multiplexer_4_out), .clk(pc_clk), .Q(pc_value[4]), .reset(pc_reset));  // open: Qn, preset
  not not_2 (not_2_out, pc_in[4]);
  Multiplexer multiplexer_5 (.in0(and_3_out), .in1(not_3_out), .out(multiplexer_5_out), .sel(pc_in_en));
  and and_3 (and_3_out, pc_en, pc_value[2], pc_value[1], pc_value[0]);
  not not_3 (not_3_out, pc_in[3]);
  Multiplexer multiplexer_6 (.in0(and_3_out), .in1(pc_in[3]), .out(multiplexer_6_out), .sel(pc_in_en));
  J_K_Flip_Flop j_k_ff_3 (
    .J(multiplexer_6_out), .K(multiplexer_5_out), .clk(pc_clk), .Q(pc_value[3]), .reset(pc_reset));  // open: Qn, preset
  and and_4 (and_4_out, pc_en, pc_value[1], pc_value[0]);
  Multiplexer multiplexer_7 (.in0(and_4_out), .in1(pc_in[2]), .out(multiplexer_7_out), .sel(pc_in_en));
  Multiplexer multiplexer_8 (.in0(and_4_out), .in1(not_4_out), .out(multiplexer_8_out), .sel(pc_in_en));
  J_K_Flip_Flop j_k_ff_4 (
    .J(multiplexer_7_out), .K(multiplexer_8_out), .clk(pc_clk), .Q(pc_value[2]), .reset(pc_reset));  // open: Qn, preset
  not not_4 (not_4_out, pc_in[2]);
  and and_5 (and_5_out, pc_en, pc_value[0]);
  Multiplexer multiplexer_9 (.in0(and_5_out), .in1(pc_in[1]), .out(multiplexer_9_out), .sel(pc_in_en));
  not not_5 (not_5_out, pc_in[1]);
  Multiplexer multiplexer_10 (.in0(and_5_out), .in1(not_5_out), .out(multiplexer_10_out), .sel(pc_in_en));
  J_K_Flip_Flop j_k_ff_5 (
    .J(multiplexer_9_out), .K(multiplexer_10_out), .clk(pc_clk), .Q(pc_value[1]), .reset(pc_reset));  // open: Qn, preset
  J_K_Flip_Flop j_k_ff_6 (
    .J(multiplexer_11_out), .K(multiplexer_12_out), .clk(pc_clk), .Q(pc_value[0]), .reset(pc_reset));  // open: Qn, preset
  not not_6 (not_6_out, pc_in[0]);
  Multiplexer multiplexer_11 (.in0(pc_en), .in1(pc_in[0]), .out(multiplexer_11_out), .sel(pc_in_en));
  Multiplexer multiplexer_12 (.in0(pc_en), .in1(not_6_out), .out(multiplexer_12_out), .sel(pc_in_en));
  assign pc_out = pc_out_en ? pc_value : 6'bz;  // Controlled_Buffer controlled_buffer_1
endmodule

module barrel_shifter (
  input  [9:0] shift_data,
  input  shift_out_en,
  input  shift_in_en,
  input  clk,
  input  [9:0] bit_amount,
  input  shift_amount_in,
  output [9:0] shift_data_out
);

  wire multiplexer_2_out, multiplexer_3_out, multiplexer_4_out, multiplexer_5_out, multiplexer_6_out,
       multiplexer_7_out, multiplexer_8_out, multiplexer_9_out, multiplexer_10_out, multiplexer_11_out,
       multiplexer_12_out, multiplexer_13_out, multiplexer_14_out, multiplexer_15_out, multiplexer_16_out,
       multiplexer_17_out, multiplexer_18_out, multiplexer_19_out, multiplexer_20_out, multiplexer_21_out,
       multiplexer_22_out, multiplexer_23_out, multiplexer_24_out, multiplexer_25_out, multiplexer_26_out,
       multiplexer_27_out, multiplexer_28_out, multiplexer_29_out, multiplexer_30_out, multiplexer_31_out;
  wire [9:0] multiplexer_1_out, multiplexer_41_out, multiplexer_42_out, reg_gp_1_reg_int_out,
       reg_gp_2_reg_int_out;

  reg_gp reg_gp_1 (
    .reg_in(shift_data), .reg_in_en(shift_in_en), .reg_clk(clk), .reg_int_out(reg_gp_1_reg_int_out));  // open: reg_out_en, reg_out
  Multiplexer #(.width(10)) multiplexer_1 (
    .in0({reg_gp_1_reg_int_out[0], reg_gp_1_reg_int_out[1], reg_gp_1_reg_int_out[2], reg_gp_1_reg_int_out[3], reg_gp_1_reg_int_out[4], reg_gp_1_reg_int_out[5], reg_gp_1_reg_int_out[6], reg_gp_1_reg_int_out[7], reg_gp_1_reg_int_out[8], reg_gp_1_reg_int_out[9]}),
    .in1(reg_gp_1_reg_int_out), .out(multiplexer_1_out), .sel(reg_gp_2_reg_int_out[4]));
  reg_gp reg_gp_2 (
    .reg_in(bit_amount), .reg_in_en(shift_amount_in), .reg_clk(clk), .reg_int_out(reg_gp_2_reg_int_out));  // open: reg_out_en, reg_out
  Multiplexer multiplexer_2 (
    .in0(multiplexer_1_out[0]), .in1(multiplexer_1_out[1]), .out(multiplexer_2_out),
    .sel(reg_gp_2_reg_int_out[0]));
  Multiplexer multiplexer_3 (
    .in0(multiplexer_1_out[1]), .in1(multiplexer_1_out[2]), .out(multiplexer_3_out),
    .sel(reg_gp_2_reg_int_out[0]));
  Multiplexer multiplexer_4 (
    .in0(multiplexer_1_out[2]), .in1(multiplexer_1_out[3]), .out(multiplexer_4_out),
    .sel(reg_gp_2_reg_int_out[0]));
  Multiplexer multiplexer_5 (
    .in0(multiplexer_1_out[3]), .in1(multiplexer_1_out[4]), .out(multiplexer_5_out),
    .sel(reg_gp_2_reg_int_out[0]));
  Multiplexer multiplexer_6 (
    .in0(multiplexer_1_out[4]), .in1(multiplexer_1_out[5]), .out(multiplexer_6_out),
    .sel(reg_gp_2_reg_int_out[0]));
  Multiplexer multiplexer_7 (
    .in0(multiplexer_1_out[5]), .in1(multiplexer_1_out[6]), .out(multiplexer_7_out),
    .sel(reg_gp_2_reg_int_out[0]));
  Multiplexer multiplexer_8 (
    .in0(multiplexer_1_out[6]), .in1(multiplexer_1_out[7]), .out(multiplexer_8_out),
    .sel(reg_gp_2_reg_int_out[0]));
  Multiplexer multiplexer_9 (
    .in0(multiplexer_1_out[7]), .in1(multiplexer_1_out[8]), .out(multiplexer_9_out),
    .sel(reg_gp_2_reg_int_out[0]));
  Multiplexer multiplexer_10 (
    .in0(multiplexer_1_out[8]), .in1(multiplexer_1_out[9]), .out(multiplexer_10_out),
    .sel(reg_gp_2_reg_int_out[0]));
  Multiplexer multiplexer_11 (
    .in0(multiplexer_1_out[9]), .in1(1'b0), .out(multiplexer_11_out), .sel(reg_gp_2_reg_int_out[0]));
  Multiplexer multiplexer_12 (
    .in0(multiplexer_2_out), .in1(multiplexer_4_out), .out(multiplexer_12_out), .sel(reg_gp_2_reg_int_out[1]));
  Multiplexer multiplexer_13 (
    .in0(multiplexer_3_out), .in1(multiplexer_5_out), .out(multiplexer_13_out), .sel(reg_gp_2_reg_int_out[1]));
  Multiplexer multiplexer_14 (
    .in0(multiplexer_4_out), .in1(multiplexer_6_out), .out(multiplexer_14_out), .sel(reg_gp_2_reg_int_out[1]));
  Multiplexer multiplexer_15 (
    .in0(multiplexer_5_out), .in1(multiplexer_7_out), .out(multiplexer_15_out), .sel(reg_gp_2_reg_int_out[1]));
  Multiplexer multiplexer_16 (
    .in0(multiplexer_6_out), .in1(multiplexer_8_out), .out(multiplexer_16_out), .sel(reg_gp_2_reg_int_out[1]));
  Multiplexer multiplexer_17 (
    .in0(multiplexer_7_out), .in1(multiplexer_9_out), .out(multiplexer_17_out), .sel(reg_gp_2_reg_int_out[1]));
  Multiplexer multiplexer_18 (
    .in0(multiplexer_8_out), .in1(multiplexer_10_out), .out(multiplexer_18_out), .sel(reg_gp_2_reg_int_out[1]));
  Multiplexer multiplexer_19 (
    .in0(multiplexer_9_out), .in1(multiplexer_11_out), .out(multiplexer_19_out), .sel(reg_gp_2_reg_int_out[1]));
  Multiplexer multiplexer_20 (
    .in0(multiplexer_10_out), .in1(1'b0), .out(multiplexer_20_out), .sel(reg_gp_2_reg_int_out[1]));
  Multiplexer multiplexer_21 (
    .in0(multiplexer_11_out), .in1(1'b0), .out(multiplexer_21_out), .sel(reg_gp_2_reg_int_out[1]));
  Multiplexer multiplexer_22 (
    .in0(multiplexer_12_out), .in1(multiplexer_16_out), .out(multiplexer_22_out),
    .sel(reg_gp_2_reg_int_out[2]));
  Multiplexer multiplexer_23 (
    .in0(multiplexer_13_out), .in1(multiplexer_17_out), .out(multiplexer_23_out),
    .sel(reg_gp_2_reg_int_out[2]));
  Multiplexer multiplexer_24 (
    .in0(multiplexer_14_out), .in1(multiplexer_18_out), .out(multiplexer_24_out),
    .sel(reg_gp_2_reg_int_out[2]));
  Multiplexer multiplexer_25 (
    .in0(multiplexer_15_out), .in1(multiplexer_19_out), .out(multiplexer_25_out),
    .sel(reg_gp_2_reg_int_out[2]));
  Multiplexer multiplexer_26 (
    .in0(multiplexer_16_out), .in1(multiplexer_20_out), .out(multiplexer_26_out),
    .sel(reg_gp_2_reg_int_out[2]));
  Multiplexer multiplexer_27 (
    .in0(multiplexer_17_out), .in1(multiplexer_21_out), .out(multiplexer_27_out),
    .sel(reg_gp_2_reg_int_out[2]));
  Multiplexer multiplexer_28 (
    .in0(multiplexer_18_out), .in1(1'b0), .out(multiplexer_28_out), .sel(reg_gp_2_reg_int_out[2]));
  Multiplexer multiplexer_29 (
    .in0(multiplexer_19_out), .in1(1'b0), .out(multiplexer_29_out), .sel(reg_gp_2_reg_int_out[2]));
  Multiplexer multiplexer_30 (
    .in0(multiplexer_20_out), .in1(1'b0), .out(multiplexer_30_out), .sel(reg_gp_2_reg_int_out[2]));
  Multiplexer multiplexer_31 (
    .in0(multiplexer_21_out), .in1(1'b0), .out(multiplexer_31_out), .sel(reg_gp_2_reg_int_out[2]));
  Multiplexer multiplexer_32 (
    .in0(multiplexer_22_out), .in1(multiplexer_30_out), .out(multiplexer_41_out[0]),
    .sel(reg_gp_2_reg_int_out[3]));
  Multiplexer multiplexer_33 (
    .in0(multiplexer_23_out), .in1(multiplexer_31_out), .out(multiplexer_41_out[1]),
    .sel(reg_gp_2_reg_int_out[3]));
  Multiplexer multiplexer_34 (
    .in0(multiplexer_24_out), .in1(1'b0), .out(multiplexer_41_out[2]), .sel(reg_gp_2_reg_int_out[3]));
  Multiplexer multiplexer_35 (
    .in0(multiplexer_25_out), .in1(1'b0), .out(multiplexer_41_out[3]), .sel(reg_gp_2_reg_int_out[3]));
  Multiplexer multiplexer_36 (
    .in0(multiplexer_26_out), .in1(1'b0), .out(multiplexer_41_out[4]), .sel(reg_gp_2_reg_int_out[3]));
  Multiplexer multiplexer_37 (
    .in0(multiplexer_27_out), .in1(1'b0), .out(multiplexer_41_out[5]), .sel(reg_gp_2_reg_int_out[3]));
  Multiplexer multiplexer_38 (
    .in0(multiplexer_28_out), .in1(1'b0), .out(multiplexer_41_out[6]), .sel(reg_gp_2_reg_int_out[3]));
  Multiplexer multiplexer_39 (
    .in0(multiplexer_29_out), .in1(1'b0), .out(multiplexer_41_out[7]), .sel(reg_gp_2_reg_int_out[3]));
  Multiplexer multiplexer_40 (
    .in0(multiplexer_30_out), .in1(1'b0), .out(multiplexer_41_out[8]), .sel(reg_gp_2_reg_int_out[3]));
  Multiplexer multiplexer_41 (
    .in0(multiplexer_31_out), .in1(1'b0), .out(multiplexer_41_out[9]), .sel(reg_gp_2_reg_int_out[3]));
  Multiplexer #(.width(10)) multiplexer_42 (
    .in0({multiplexer_41_out[0], multiplexer_41_out[1], multiplexer_41_out[2], multiplexer_41_out[3], multiplexer_41_out[4], multiplexer_41_out[5], multiplexer_41_out[6], multiplexer_41_out[7], multiplexer_41_out[8], multiplexer_41_out[9]}),
    .in1(multiplexer_41_out), .out(multiplexer_42_out), .sel(reg_gp_2_reg_int_out[4]));
  assign shift_data_out = shift_out_en ? multiplexer_42_out : 10'bz;  // Controlled_Buffer controlled_buffer_1
endmodule

module ring_rotator (
  input  [9:0] rotate_data,
  input  rotate_out_en,
  input  rotate_in_en,
  input  clk,
  input  [9:0] bit_amount,
  input  rotate_amount_in,
  output [9:0] rotate_data_out
);

  wire multiplexer_2_out, multiplexer_3_out, multiplexer_4_out, multiplexer_5_out, multiplexer_6_out,
       multiplexer_7_out, multiplexer_8_out, multiplexer_9_out, multiplexer_10_out, multiplexer_11_out,
       multiplexer_12_out, multiplexer_13_out, multiplexer_14_out, multiplexer_15_out, multiplexer_16_out,
       multiplexer_17_out, multiplexer_18_out, multiplexer_19_out, multiplexer_20_out, multiplexer_21_out,
       multiplexer_22_out, multiplexer_23_out, multiplexer_24_out, multiplexer_25_out, multiplexer_26_out,
       multiplexer_27_out, multiplexer_28_out, multiplexer_29_out, multiplexer_30_out, multiplexer_31_out;
  wire [9:0] multiplexer_1_out, multiplexer_41_out, multiplexer_42_out, reg_gp_1_reg_int_out,
       reg_gp_2_reg_int_out;

  reg_gp reg_gp_1 (
    .reg_in(rotate_data), .reg_in_en(rotate_in_en), .reg_clk(clk), .reg_int_out(reg_gp_1_reg_int_out));  // open: reg_out_en, reg_out
  Multiplexer #(.width(10)) multiplexer_1 (
    .in0({reg_gp_1_reg_int_out[0], reg_gp_1_reg_int_out[1], reg_gp_1_reg_int_out[2], reg_gp_1_reg_int_out[3], reg_gp_1_reg_int_out[4], reg_gp_1_reg_int_out[5], reg_gp_1_reg_int_out[6], reg_gp_1_reg_int_out[7], reg_gp_1_reg_int_out[8], reg_gp_1_reg_int_out[9]}),
    .in1(reg_gp_1_reg_int_out), .out(multiplexer_1_out), .sel(reg_gp_2_reg_int_out[4]));
  reg_gp reg_gp_2 (
    .reg_in(bit_amount), .reg_in_en(rotate_amount_in), .reg_clk(clk), .reg_int_out(reg_gp_2_reg_int_out));  // open: reg_out_en, reg_out
  Multiplexer multiplexer_2 (
    .in0(multiplexer_1_out[0]), .in1(multiplexer_1_out[1]), .out(multiplexer_2_out),
    .sel(reg_gp_2_reg_int_out[0]));
  Multiplexer multiplexer_3 (
    .in0(multiplexer_1_out[1]), .in1(multiplexer_1_out[2]), .out(multiplexer_3_out),
    .sel(reg_gp_2_reg_int_out[0]));
  Multiplexer multiplexer_4 (
    .in0(multiplexer_1_out[2]), .in1(multiplexer_1_out[3]), .out(multiplexer_4_out),
    .sel(reg_gp_2_reg_int_out[0]));
  Multiplexer multiplexer_5 (
    .in0(multiplexer_1_out[3]), .in1(multiplexer_1_out[4]), .out(multiplexer_5_out),
    .sel(reg_gp_2_reg_int_out[0]));
  Multiplexer multiplexer_6 (
    .in0(multiplexer_1_out[4]), .in1(multiplexer_1_out[5]), .out(multiplexer_6_out),
    .sel(reg_gp_2_reg_int_out[0]));
  Multiplexer multiplexer_7 (
    .in0(multiplexer_1_out[5]), .in1(multiplexer_1_out[6]), .out(multiplexer_7_out),
    .sel(reg_gp_2_reg_int_out[0]));
  Multiplexer multiplexer_8 (
    .in0(multiplexer_1_out[6]), .in1(multiplexer_1_out[7]), .out(multiplexer_8_out),
    .sel(reg_gp_2_reg_int_out[0]));
  Multiplexer multiplexer_9 (
    .in0(multiplexer_1_out[7]), .in1(multiplexer_1_out[8]), .out(multiplexer_9_out),
    .sel(reg_gp_2_reg_int_out[0]));
  Multiplexer multiplexer_10 (
    .in0(multiplexer_1_out[8]), .in1(multiplexer_1_out[9]), .out(multiplexer_10_out),
    .sel(reg_gp_2_reg_int_out[0]));
  Multiplexer multiplexer_11 (
    .in0(multiplexer_1_out[9]), .in1(multiplexer_1_out[0]), .out(multiplexer_11_out),
    .sel(reg_gp_2_reg_int_out[0]));
  Multiplexer multiplexer_12 (
    .in0(multiplexer_2_out), .in1(multiplexer_4_out), .out(multiplexer_12_out), .sel(reg_gp_2_reg_int_out[1]));
  Multiplexer multiplexer_13 (
    .in0(multiplexer_3_out), .in1(multiplexer_5_out), .out(multiplexer_13_out), .sel(reg_gp_2_reg_int_out[1]));
  Multiplexer multiplexer_14 (
    .in0(multiplexer_4_out), .in1(multiplexer_6_out), .out(multiplexer_14_out), .sel(reg_gp_2_reg_int_out[1]));
  Multiplexer multiplexer_15 (
    .in0(multiplexer_5_out), .in1(multiplexer_7_out), .out(multiplexer_15_out), .sel(reg_gp_2_reg_int_out[1]));
  Multiplexer multiplexer_16 (
    .in0(multiplexer_6_out), .in1(multiplexer_8_out), .out(multiplexer_16_out), .sel(reg_gp_2_reg_int_out[1]));
  Multiplexer multiplexer_17 (
    .in0(multiplexer_7_out), .in1(multiplexer_9_out), .out(multiplexer_17_out), .sel(reg_gp_2_reg_int_out[1]));
  Multiplexer multiplexer_18 (
    .in0(multiplexer_8_out), .in1(multiplexer_10_out), .out(multiplexer_18_out), .sel(reg_gp_2_reg_int_out[1]));
  Multiplexer multiplexer_19 (
    .in0(multiplexer_9_out), .in1(multiplexer_11_out), .out(multiplexer_19_out), .sel(reg_gp_2_reg_int_out[1]));
  Multiplexer multiplexer_20 (
    .in0(multiplexer_10_out), .in1(multiplexer_2_out), .out(multiplexer_20_out), .sel(reg_gp_2_reg_int_out[1]));
  Multiplexer multiplexer_21 (
    .in0(multiplexer_11_out), .in1(multiplexer_3_out), .out(multiplexer_21_out), .sel(reg_gp_2_reg_int_out[1]));
  Multiplexer multiplexer_22 (
    .in0(multiplexer_12_out), .in1(multiplexer_16_out), .out(multiplexer_22_out),
    .sel(reg_gp_2_reg_int_out[2]));
  Multiplexer multiplexer_23 (
    .in0(multiplexer_13_out), .in1(multiplexer_17_out), .out(multiplexer_23_out),
    .sel(reg_gp_2_reg_int_out[2]));
  Multiplexer multiplexer_24 (
    .in0(multiplexer_14_out), .in1(multiplexer_18_out), .out(multiplexer_24_out),
    .sel(reg_gp_2_reg_int_out[2]));
  Multiplexer multiplexer_25 (
    .in0(multiplexer_15_out), .in1(multiplexer_19_out), .out(multiplexer_25_out),
    .sel(reg_gp_2_reg_int_out[2]));
  Multiplexer multiplexer_26 (
    .in0(multiplexer_16_out), .in1(multiplexer_20_out), .out(multiplexer_26_out),
    .sel(reg_gp_2_reg_int_out[2]));
  Multiplexer multiplexer_27 (
    .in0(multiplexer_17_out), .in1(multiplexer_21_out), .out(multiplexer_27_out),
    .sel(reg_gp_2_reg_int_out[2]));
  Multiplexer multiplexer_28 (
    .in0(multiplexer_18_out), .in1(multiplexer_12_out), .out(multiplexer_28_out),
    .sel(reg_gp_2_reg_int_out[2]));
  Multiplexer multiplexer_29 (
    .in0(multiplexer_19_out), .in1(multiplexer_13_out), .out(multiplexer_29_out),
    .sel(reg_gp_2_reg_int_out[2]));
  Multiplexer multiplexer_30 (
    .in0(multiplexer_20_out), .in1(multiplexer_14_out), .out(multiplexer_30_out),
    .sel(reg_gp_2_reg_int_out[2]));
  Multiplexer multiplexer_31 (
    .in0(multiplexer_21_out), .in1(multiplexer_15_out), .out(multiplexer_31_out),
    .sel(reg_gp_2_reg_int_out[2]));
  Multiplexer multiplexer_32 (
    .in0(multiplexer_22_out), .in1(multiplexer_30_out), .out(multiplexer_41_out[0]),
    .sel(reg_gp_2_reg_int_out[3]));
  Multiplexer multiplexer_33 (
    .in0(multiplexer_23_out), .in1(multiplexer_31_out), .out(multiplexer_41_out[1]),
    .sel(reg_gp_2_reg_int_out[3]));
  Multiplexer multiplexer_34 (
    .in0(multiplexer_24_out), .in1(multiplexer_22_out), .out(multiplexer_41_out[2]),
    .sel(reg_gp_2_reg_int_out[3]));
  Multiplexer multiplexer_35 (
    .in0(multiplexer_25_out), .in1(multiplexer_23_out), .out(multiplexer_41_out[3]),
    .sel(reg_gp_2_reg_int_out[3]));
  Multiplexer multiplexer_36 (
    .in0(multiplexer_26_out), .in1(multiplexer_24_out), .out(multiplexer_41_out[4]),
    .sel(reg_gp_2_reg_int_out[3]));
  Multiplexer multiplexer_37 (
    .in0(multiplexer_27_out), .in1(multiplexer_25_out), .out(multiplexer_41_out[5]),
    .sel(reg_gp_2_reg_int_out[3]));
  Multiplexer multiplexer_38 (
    .in0(multiplexer_28_out), .in1(multiplexer_26_out), .out(multiplexer_41_out[6]),
    .sel(reg_gp_2_reg_int_out[3]));
  Multiplexer multiplexer_39 (
    .in0(multiplexer_29_out), .in1(multiplexer_27_out), .out(multiplexer_41_out[7]),
    .sel(reg_gp_2_reg_int_out[3]));
  Multiplexer multiplexer_40 (
    .in0(multiplexer_30_out), .in1(multiplexer_28_out), .out(multiplexer_41_out[8]),
    .sel(reg_gp_2_reg_int_out[3]));
  Multiplexer multiplexer_41 (
    .in0(multiplexer_31_out), .in1(multiplexer_29_out), .out(multiplexer_41_out[9]),
    .sel(reg_gp_2_reg_int_out[3]));
  Multiplexer #(.width(10)) multiplexer_42 (
    .in0({multiplexer_41_out[0], multiplexer_41_out[1], multiplexer_41_out[2], multiplexer_41_out[3], multiplexer_41_out[4], multiplexer_41_out[5], multiplexer_41_out[6], multiplexer_41_out[7], multiplexer_41_out[8], multiplexer_41_out[9]}),
    .in1(multiplexer_41_out), .out(multiplexer_42_out), .sel(reg_gp_2_reg_int_out[4]));
  assign rotate_data_out = rotate_out_en ? multiplexer_42_out : 10'bz;  // Controlled_Buffer controlled_buffer_1
endmodule
