// Logisim project lab1_practice.circ as structural Verilog: 14 circuits, main circuit main
module main (
  input  in_1,
  input  in_2,
  input  in_3,
  output [3:0] out_4,
  output [7:0] out_5,
  output [7:0] out_6,
  output [7:0] out_7,
  output [7:0] out_8,
  output [3:0] out_9,
  output zero_flag,
  output overflow_flag,
  output carry_flag,
  output sign_flag,
  output [7:0] reg_0,
  output [7:0] out_15,
  output [7:0] reg_1,
  output [7:0] reg_2,
  output [7:0] reg_3,
  output [7:0] reg_4,
  output [7:0] reg_5,
  output [7:0] reg_6,
  output [7:0] reg_7,
  output [7:0] reg_8,
  output [7:0] reg_9,
  output [7:0] reg_10,
  output [7:0] out_26,
  output [7:0] reg_11,
  output [3:0] out_28,
  output [7:0] reg_12,
  output [3:0] out_30,
  output [7:0] reg_13,
  output [7:0] reg_14,
  output [7:0] reg_15,
  output [3:0] out_34,
  output [7:0] out_35
);

  wire a_in, a_out, alu_out, alu_sub, b_in, b_out, clk, decoder_1_out15, flag_clk, ins_reg_in_en,
       ins_reg_out_en, mar_in_en, multiplexer_1_out, pc_en, pc_in_en, pc_out, pull_resistor_1_node,
       pull_resistor_2_node, pull_resistor_4_node, ram_rd, sram_rd, sram_wr;
  wire [7:0] ram_1_dout;
  wire [7:4] reg_gp_3_reg_int_out;
  wire [7:7] pull_resistor_3_node;

  Pull_Resistor pull_resistor_1 (.node(pull_resistor_1_node));
  Multiplexer multiplexer_1 (.in0(pc_en), .in1(pull_resistor_1_node), .out(multiplexer_1_out), .sel(decoder_1_out15));
  Decoder #(.select(4)) decoder_1 (
    .out15(decoder_1_out15), .sel(out_9), .en(pull_resistor_2_node));  // open: out0, out1, out2, out3, out4, out5, out6, out7, out8, out9, out10, out11, out12, out13, out14
  pc pc_1 (
    .pc_en(multiplexer_1_out), .pc_in(out_28), .pc_in_en(pc_in_en), .pc_reset(in_1), .pc_clk(clk),
    .pc_out_en(pc_out), .pc_value(out_9), .pc_out(out_28));
  Pull_Resistor #(.pull(1)) pull_resistor_2 (.node(pull_resistor_2_node));
  sram sram_1 (
    .sram_d_in({out_35[7:4], out_28}), .sram_wr(sram_wr), .sram_rd(sram_rd),
    .mar_d_in({out_35[7:4], out_28}), .mar_in_en(mar_in_en), .sram_clk(clk),
    .sram_d_out({out_35[7:4], out_28}), .out_8(reg_0), .out_9(reg_1), .out_10(reg_2), .out_11(reg_3),
    .out_12(reg_4), .out_13(reg_5), .out_14(reg_6), .out_15(reg_7), .out_16(reg_8), .out_17(reg_9),
    .out_18(reg_10), .out_19(reg_11), .out_20(reg_12), .out_21(reg_13), .out_22(reg_14), .out_23(reg_15));
  assign {out_35[7:4], out_28} = in_3 ? out_5 : 8'bz;  // Controlled_Buffer controlled_buffer_1
  Clock clock_1 (.out(clk));
  assign out_6 = in_3 ? {out_35[7:4], out_28} : 8'bz;  // Controlled_Buffer controlled_buffer_2
  reg_gp reg_gp_1 (
    .reg_in({out_35[7:4], out_28}), .reg_in_en(a_in), .reg_clk(clk), .reg_out_en(a_out), .reg_int_out(out_8),
    .reg_out({out_35[7:4], out_28}));
  reg_gp reg_gp_2 (
    .reg_in({out_35[7:4], out_28}), .reg_in_en(b_in), .reg_clk(clk), .reg_out_en(b_out),
    .reg_int_out(out_15), .reg_out({out_35[7:4], out_28}));
  ins_reg ins_reg_1 (
    .ins_reg_in({out_35[7:4], out_28}), .ins_reg_in_en(ins_reg_in_en), .clk(clk),
    .ins_reg_out_en(ins_reg_out_en), .out_5(out_26), .add_outs(out_28), .ins_out(out_30));
  // RGBLED rgbled_1: pin names not known; wires that end beside it: out_8[1], out_8[0], out_8[2]
  reg_gp reg_gp_3 (
    .reg_in(out_6), .reg_in_en(mar_in_en), .reg_clk(clk), .reg_int_out({reg_gp_3_reg_int_out, out_4}));  // open: reg_out_en, reg_out
  alu alu_1 (
    .alu_in_1(out_8), .alu_out_en(alu_out), .alu_sub(alu_sub), .alu_in_2(out_15), .alu_zero_out(zero_flag),
    .alu_overflow_out(overflow_flag), .alu_carry_out(carry_flag), .alu_out({out_35[7:4], out_28}),
    .alu_sign_out(sign_flag));
  RAM #(.addrWidth(4), .trigger("falling")) ram_1 (
    .addr(out_4), .oe(ram_rd), .clk(clk), .dout(ram_1_dout));  // open: we, din
  Pull_Resistor pull_resistor_3 (.node(pull_resistor_3_node[7]));
  cs cs_1 (
    .debug(in_3), .clk(clk), .ring_reset(in_2), .data_in(out_30), .flag_reg(out_7), .pc_en(pc_en),
    .pc_out(pc_out), .pc_reset(in_1), .sram_wr(sram_wr), .out_10(out_34), .sram_rd(sram_rd),
    .mar_in_en(mar_in_en), .ins_reg_in_en(ins_reg_in_en), .ins_reg_out_en(ins_reg_out_en), .a_in(a_in),
    .a_out(a_out), .alu_out(alu_out), .alu_sub(alu_sub), .b_in(b_in), .b_out(b_out), .ram_rd(ram_rd),
    .pc_in_en(pc_in_en), .flag_clk(flag_clk));
  Pull_Resistor #(.pull(1)) pull_resistor_4 (.node(pull_resistor_4_node));
  assign out_5 = ram_rd ? ram_1_dout : 8'bz;  // Controlled_Buffer controlled_buffer_3
  reg_gp flag_reg (
    .reg_in({{4{pull_resistor_3_node[7]}}, sign_flag, carry_flag, overflow_flag, zero_flag}),
    .reg_in_en(pull_resistor_4_node), .reg_clk(flag_clk), .reg_int_out(out_7));  // open: reg_out_en, reg_out

  assign out_35[3:0] = out_28;

  // Other names for the same wires on the sheet: debug = in_3; debug_data[7:0] = out_5;
  //   debug_data_out[7:0] = {out_35[7:4], out_28}; flag_out[7:0] = out_7; pc_reset = in_1; ring_reset = in_2

  // Notes on the sheet:
  //   Clock
  //   Debug & Testing
  //   Green: A=B
  //   Red: A>B
  //   Blue: A<B
  //   s c o z
  //   0. Debug
  //   1. LDA
  //   2. LDB
  //   3. OUT
  //   4. SUB
  //   5. HLT
  //   6. LDI
  //   7. STA
  //   8. CMP
  //   9. JMP
  //   10. JNZ
  //   11. JNC
endmodule

module reg_gp (
  input  [7:0] reg_in,
  input  reg_in_en,
  input  reg_clk,
  input  reg_out_en,
  output [7:0] reg_int_out,
  output [7:0] reg_out
);

  wire multiplexer_1_out, multiplexer_2_out, multiplexer_3_out, multiplexer_4_out, multiplexer_5_out,
       multiplexer_6_out, multiplexer_7_out, multiplexer_8_out;

  Multiplexer multiplexer_1 (.in0(reg_int_out[7]), .in1(reg_in[7]), .out(multiplexer_1_out), .sel(reg_in_en));
  D_Flip_Flop d_ff_1 (.D(multiplexer_1_out), .clk(reg_clk), .Q(reg_int_out[7]));  // open: Qn, preset, reset
  assign reg_out[7] = reg_out_en ? reg_int_out[7] : 1'bz;  // Controlled_Buffer controlled_buffer_1
  Multiplexer multiplexer_2 (.in0(reg_int_out[6]), .in1(reg_in[6]), .out(multiplexer_2_out), .sel(reg_in_en));
  D_Flip_Flop d_ff_2 (.D(multiplexer_2_out), .clk(reg_clk), .Q(reg_int_out[6]));  // open: Qn, preset, reset
  Multiplexer multiplexer_3 (.in0(reg_int_out[5]), .in1(reg_in[5]), .out(multiplexer_3_out), .sel(reg_in_en));
  assign reg_out[6] = reg_out_en ? reg_int_out[6] : 1'bz;  // Controlled_Buffer controlled_buffer_2
  Multiplexer multiplexer_4 (.in0(reg_int_out[4]), .in1(reg_in[4]), .out(multiplexer_4_out), .sel(reg_in_en));
  D_Flip_Flop d_ff_3 (.D(multiplexer_3_out), .clk(reg_clk), .Q(reg_int_out[5]));  // open: Qn, preset, reset
  Multiplexer multiplexer_5 (.in0(reg_int_out[3]), .in1(reg_in[3]), .out(multiplexer_5_out), .sel(reg_in_en));
  D_Flip_Flop d_ff_4 (.D(multiplexer_4_out), .clk(reg_clk), .Q(reg_int_out[4]));  // open: Qn, preset, reset
  assign reg_out[5] = reg_out_en ? reg_int_out[5] : 1'bz;  // Controlled_Buffer controlled_buffer_3
  assign reg_out[4] = reg_out_en ? reg_int_out[4] : 1'bz;  // Controlled_Buffer controlled_buffer_4
  Multiplexer multiplexer_6 (.in0(reg_int_out[2]), .in1(reg_in[2]), .out(multiplexer_6_out), .sel(reg_in_en));
  D_Flip_Flop d_ff_5 (.D(multiplexer_5_out), .clk(reg_clk), .Q(reg_int_out[3]));  // open: Qn, preset, reset
  Multiplexer multiplexer_7 (.in0(reg_int_out[1]), .in1(reg_in[1]), .out(multiplexer_7_out), .sel(reg_in_en));
  assign reg_out[3] = reg_out_en ? reg_int_out[3] : 1'bz;  // Controlled_Buffer controlled_buffer_5
  Multiplexer multiplexer_8 (.in0(reg_int_out[0]), .in1(reg_in[0]), .out(multiplexer_8_out), .sel(reg_in_en));
  D_Flip_Flop d_ff_6 (.D(multiplexer_6_out), .clk(reg_clk), .Q(reg_int_out[2]));  // open: Qn, preset, reset
  D_Flip_Flop d_ff_7 (.D(multiplexer_7_out), .clk(reg_clk), .Q(reg_int_out[1]));  // open: Qn, preset, reset
  assign reg_out[2] = reg_out_en ? reg_int_out[2] : 1'bz;  // Controlled_Buffer controlled_buffer_6
  assign reg_out[1] = reg_out_en ? reg_int_out[1] : 1'bz;  // Controlled_Buffer controlled_buffer_7
  D_Flip_Flop d_ff_8 (.D(multiplexer_8_out), .clk(reg_clk), .Q(reg_int_out[0]));  // open: Qn, preset, reset
  assign reg_out[0] = reg_out_en ? reg_int_out[0] : 1'bz;  // Controlled_Buffer controlled_buffer_8
endmodule

module alu (
  input  [7:0] alu_in_1,
  input  alu_out_en,
  input  alu_sub,
  input  [7:0] alu_in_2,
  output alu_zero_out,
  output alu_overflow_out,
  output alu_carry_out,
  output [7:0] alu_out,
  output alu_sign_out
);

  wire adder_2_cout, adder_3_cout, adder_4_cout, adder_5_cout, adder_6_cout, adder_7_cout, adder_8_cout,
       xor_2_out, xor_3_out, xor_4_out, xor_5_out, xor_6_out, xor_7_out, xor_8_out, xor_9_out;
  wire [6:0] adder_8_out;

  xor xor_1 (alu_overflow_out, adder_2_cout, alu_carry_out);
  xor xor_2 (xor_2_out, alu_sub, alu_in_2[7]);
  Adder #(.width(1)) adder_1 (
    .a(alu_in_1[7]), .b(xor_2_out), .out(alu_sign_out), .cin(adder_2_cout), .cout(alu_carry_out));
  Adder #(.width(1)) adder_2 (
    .a(alu_in_1[6]), .b(xor_3_out), .out(adder_8_out[6]), .cin(adder_3_cout), .cout(adder_2_cout));
  xor xor_3 (xor_3_out, alu_sub, alu_in_2[6]);
  xor xor_4 (xor_4_out, alu_sub, alu_in_2[5]);
  Adder #(.width(1)) adder_3 (
    .a(alu_in_1[5]), .b(xor_4_out), .out(adder_8_out[5]), .cin(adder_4_cout), .cout(adder_3_cout));
  Adder #(.width(1)) adder_4 (
    .a(alu_in_1[4]), .b(xor_5_out), .out(adder_8_out[4]), .cin(adder_5_cout), .cout(adder_4_cout));
  xor xor_5 (xor_5_out, alu_sub, alu_in_2[4]);
  xor xor_6 (xor_6_out, alu_sub, alu_in_2[3]);
  Adder #(.width(1)) adder_5 (
    .a(alu_in_1[3]), .b(xor_6_out), .out(adder_8_out[3]), .cin(adder_6_cout), .cout(adder_5_cout));
  Adder #(.width(1)) adder_6 (
    .a(alu_in_1[2]), .b(xor_7_out), .out(adder_8_out[2]), .cin(adder_7_cout), .cout(adder_6_cout));
  xor xor_7 (xor_7_out, alu_sub, alu_in_2[2]);
  xor xor_8 (xor_8_out, alu_sub, alu_in_2[1]);
  Adder #(.width(1)) adder_7 (
    .a(alu_in_1[1]), .b(xor_8_out), .out(adder_8_out[1]), .cin(adder_8_cout), .cout(adder_7_cout));
  Adder #(.width(1)) adder_8 (.a(alu_in_1[0]), .b(xor_9_out), .out(adder_8_out[0]), .cin(alu_sub), .cout(adder_8_cout));
  xor xor_9 (xor_9_out, alu_sub, alu_in_2[0]);
  nor nor_1 (alu_zero_out, adder_8_out[0], adder_8_out[1], adder_8_out[2], adder_8_out[3], adder_8_out[4], adder_8_out[5], adder_8_out[6], alu_sign_out);
  assign alu_out = alu_out_en ? {alu_sign_out, adder_8_out} : 8'bz;  // Controlled_Buffer controlled_buffer_1
endmodule

module pc_copy (
  input  [3:0] pc_in,
  input  pc_en,
  input  pc_in_en,
  input  pc_clk,
  input  pc_reset,
  input  pc_out_en,
  output [3:0] pc_value,
  output [3:0] pc_out
);

  wire j_k_ff_2_qn, j_k_ff_3_qn, j_k_ff_4_qn, multiplexer_1_out, multiplexer_2_out, multiplexer_3_out,
       multiplexer_4_out, multiplexer_5_out, multiplexer_6_out, multiplexer_7_out, multiplexer_8_out,
       multiplexer_9_out, multiplexer_10_out, multiplexer_11_out, not_1_out, not_2_out, not_3_out, not_4_out;

  Multiplexer multiplexer_1 (.in0(pc_en), .in1(pc_in[3]), .out(multiplexer_1_out), .sel(pc_in_en));
  not not_1 (not_1_out, pc_in[3]);
  Multiplexer multiplexer_2 (.in0(pc_en), .in1(not_1_out), .out(multiplexer_2_out), .sel(pc_in_en));
  J_K_Flip_Flop j_k_ff_1 (
    .J(multiplexer_1_out), .K(multiplexer_2_out), .clk(multiplexer_4_out), .Q(pc_value[3]), .reset(pc_reset));  // open: Qn, preset
  not not_2 (not_2_out, pc_in[2]);
  Multiplexer multiplexer_3 (.in0(pc_en), .in1(not_2_out), .out(multiplexer_3_out), .sel(pc_in_en));
  Multiplexer multiplexer_4 (.in0(j_k_ff_2_qn), .in1(pc_clk), .out(multiplexer_4_out), .sel(pc_in_en));
  Multiplexer multiplexer_5 (.in0(pc_en), .in1(pc_in[2]), .out(multiplexer_5_out), .sel(pc_in_en));
  J_K_Flip_Flop j_k_ff_2 (
    .J(multiplexer_5_out), .K(multiplexer_3_out), .clk(multiplexer_7_out), .Q(pc_value[2]), .Qn(j_k_ff_2_qn),
    .reset(pc_reset));  // open: preset
  Multiplexer multiplexer_6 (.in0(pc_en), .in1(not_3_out), .out(multiplexer_6_out), .sel(pc_in_en));
  Multiplexer multiplexer_7 (.in0(j_k_ff_3_qn), .in1(pc_clk), .out(multiplexer_7_out), .sel(pc_in_en));
  Multiplexer multiplexer_8 (.in0(pc_en), .in1(pc_in[1]), .out(multiplexer_8_out), .sel(pc_in_en));
  not not_3 (not_3_out, pc_in[1]);
  J_K_Flip_Flop j_k_ff_3 (
    .J(multiplexer_8_out), .K(multiplexer_6_out), .clk(multiplexer_9_out), .Q(pc_value[1]), .Qn(j_k_ff_3_qn),
    .reset(pc_reset));  // open: preset
  Multiplexer multiplexer_9 (.in0(j_k_ff_4_qn), .in1(pc_clk), .out(multiplexer_9_out), .sel(pc_in_en));
  Multiplexer multiplexer_10 (.in0(pc_en), .in1(pc_in[0]), .out(multiplexer_10_out), .sel(pc_in_en));
  not not_4 (not_4_out, pc_in[0]);
  Multiplexer multiplexer_11 (.in0(pc_en), .in1(not_4_out), .out(multiplexer_11_out), .sel(pc_in_en));
  J_K_Flip_Flop j_k_ff_4 (
    .J(multiplexer_10_out), .K(multiplexer_11_out), .clk(pc_clk), .Q(pc_value[0]), .Qn(j_k_ff_4_qn),
    .reset(pc_reset));  // open: preset
  assign pc_out = pc_out_en ? pc_value : 4'bz;  // Controlled_Buffer controlled_buffer_1
endmodule

module dec_4x16 (
  input  [3:0] dec_sel,
  output [15:0] dec_out
);

  wire not_1_out, not_2_out, not_3_out, not_4_out;

  not not_1 (not_1_out, dec_sel[3]);
  not not_2 (not_2_out, dec_sel[2]);
  not not_3 (not_3_out, dec_sel[1]);
  not not_4 (not_4_out, dec_sel[0]);
  and and_1 (dec_out[0], not_4_out, not_3_out, not_2_out, not_1_out);
  and and_2 (dec_out[1], dec_sel[0], not_3_out, not_2_out, not_1_out);
  and and_3 (dec_out[2], not_4_out, dec_sel[1], not_2_out, not_1_out);
  and and_4 (dec_out[3], dec_sel[0], dec_sel[1], not_2_out, not_1_out);
  and and_5 (dec_out[4], not_4_out, not_3_out, dec_sel[2], not_1_out);
  and and_6 (dec_out[5], dec_sel[0], not_3_out, dec_sel[2], not_1_out);
  and and_7 (dec_out[6], not_4_out, dec_sel[1], dec_sel[2], not_1_out);
  and and_8 (dec_out[7], dec_sel[0], dec_sel[1], dec_sel[2], not_1_out);
  and and_9 (dec_out[8], not_4_out, not_3_out, not_2_out, dec_sel[3]);
  and and_10 (dec_out[9], dec_sel[0], not_3_out, not_2_out, dec_sel[3]);
  and and_11 (dec_out[10], not_4_out, dec_sel[1], not_2_out, dec_sel[3]);
  and and_12 (dec_out[11], dec_sel[0], dec_sel[1], not_2_out, dec_sel[3]);
  and and_13 (dec_out[12], not_4_out, not_3_out, dec_sel[2], dec_sel[3]);
  and and_14 (dec_out[13], dec_sel[0], not_3_out, dec_sel[2], dec_sel[3]);
  and and_15 (dec_out[14], not_4_out, dec_sel[1], dec_sel[2], dec_sel[3]);
  and and_16 (dec_out[15], dec_sel[0], dec_sel[1], dec_sel[2], dec_sel[3]);
endmodule

module sram_cell (
  input  [7:0] data_in,
  input  wr_en,
  input  clk,
  input  cs,
  input  rd_en,
  output [7:0] memory_content,
  output [7:0] data_out
);

  wire and_1_out, and_2_out;

  and and_1 (and_1_out, wr_en, cs);
  and and_2 (and_2_out, cs, rd_en);
  reg_gp reg_gp_1 (
    .reg_in(data_in), .reg_in_en(and_1_out), .reg_clk(clk), .reg_out_en(and_2_out),
    .reg_int_out(memory_content), .reg_out(data_out));
endmodule

module sram (
  input  [7:0] sram_d_in,
  input  sram_wr,
  input  sram_rd,
  input  [7:0] mar_d_in,
  input  mar_in_en,
  input  sram_clk,
  output [7:0] sram_d_out,
  output [7:0] out_8,
  output [7:0] out_9,
  output [7:0] out_10,
  output [7:0] out_11,
  output [7:0] out_12,
  output [7:0] out_13,
  output [7:0] out_14,
  output [7:0] out_15,
  output [7:0] out_16,
  output [7:0] out_17,
  output [7:0] out_18,
  output [7:0] out_19,
  output [7:0] out_20,
  output [7:0] out_21,
  output [7:0] out_22,
  output [7:0] out_23
);

  wire [7:0] controlled_buffer_1_out, reg_gp_1_reg_int_out;
  wire [15:0] dec_4x16_1_dec_out;

  reg_gp reg_gp_1 (
    .reg_in(mar_d_in), .reg_in_en(mar_in_en), .reg_clk(sram_clk), .reg_int_out(reg_gp_1_reg_int_out));  // open: reg_out_en, reg_out
  dec_4x16 dec_4x16_1 (.dec_sel(reg_gp_1_reg_int_out[3:0]), .dec_out(dec_4x16_1_dec_out));
  assign controlled_buffer_1_out = sram_wr ? sram_d_in : 8'bz;  // Controlled_Buffer controlled_buffer_1
  sram_cell sram_cell_1 (
    .data_in(controlled_buffer_1_out), .wr_en(sram_wr), .clk(sram_clk), .cs(dec_4x16_1_dec_out[0]),
    .rd_en(sram_rd), .memory_content(out_8), .data_out(controlled_buffer_1_out));
  sram_cell sram_cell_2 (
    .data_in(controlled_buffer_1_out), .wr_en(sram_wr), .clk(sram_clk), .cs(dec_4x16_1_dec_out[1]),
    .rd_en(sram_rd), .memory_content(out_9), .data_out(controlled_buffer_1_out));
  sram_cell sram_cell_3 (
    .data_in(controlled_buffer_1_out), .wr_en(sram_wr), .clk(sram_clk), .cs(dec_4x16_1_dec_out[2]),
    .rd_en(sram_rd), .memory_content(out_10), .data_out(controlled_buffer_1_out));
  sram_cell sram_cell_4 (
    .data_in(controlled_buffer_1_out), .wr_en(sram_wr), .clk(sram_clk), .cs(dec_4x16_1_dec_out[3]),
    .rd_en(sram_rd), .memory_content(out_11), .data_out(controlled_buffer_1_out));
  sram_cell sram_cell_5 (
    .data_in(controlled_buffer_1_out), .wr_en(sram_wr), .clk(sram_clk), .cs(dec_4x16_1_dec_out[4]),
    .rd_en(sram_rd), .memory_content(out_12), .data_out(controlled_buffer_1_out));
  sram_cell sram_cell_6 (
    .data_in(controlled_buffer_1_out), .wr_en(sram_wr), .clk(sram_clk), .cs(dec_4x16_1_dec_out[5]),
    .rd_en(sram_rd), .memory_content(out_13), .data_out(controlled_buffer_1_out));
  sram_cell sram_cell_7 (
    .data_in(controlled_buffer_1_out), .wr_en(sram_wr), .clk(sram_clk), .cs(dec_4x16_1_dec_out[6]),
    .rd_en(sram_rd), .memory_content(out_14), .data_out(controlled_buffer_1_out));
  sram_cell sram_cell_8 (
    .data_in(controlled_buffer_1_out), .wr_en(sram_wr), .clk(sram_clk), .cs(dec_4x16_1_dec_out[7]),
    .rd_en(sram_rd), .memory_content(out_15), .data_out(controlled_buffer_1_out));
  sram_cell sram_cell_9 (
    .data_in(controlled_buffer_1_out), .wr_en(sram_wr), .clk(sram_clk), .cs(dec_4x16_1_dec_out[8]),
    .rd_en(sram_rd), .memory_content(out_16), .data_out(controlled_buffer_1_out));
  sram_cell sram_cell_10 (
    .data_in(controlled_buffer_1_out), .wr_en(sram_wr), .clk(sram_clk), .cs(dec_4x16_1_dec_out[9]),
    .rd_en(sram_rd), .memory_content(out_17), .data_out(controlled_buffer_1_out));
  sram_cell sram_cell_11 (
    .data_in(controlled_buffer_1_out), .wr_en(sram_wr), .clk(sram_clk), .cs(dec_4x16_1_dec_out[10]),
    .rd_en(sram_rd), .memory_content(out_18), .data_out(controlled_buffer_1_out));
  sram_cell sram_cell_12 (
    .data_in(controlled_buffer_1_out), .wr_en(sram_wr), .clk(sram_clk), .cs(dec_4x16_1_dec_out[11]),
    .rd_en(sram_rd), .memory_content(out_19), .data_out(controlled_buffer_1_out));
  sram_cell sram_cell_13 (
    .data_in(controlled_buffer_1_out), .wr_en(sram_wr), .clk(sram_clk), .cs(dec_4x16_1_dec_out[12]),
    .rd_en(sram_rd), .memory_content(out_20), .data_out(controlled_buffer_1_out));
  sram_cell sram_cell_14 (
    .data_in(controlled_buffer_1_out), .wr_en(sram_wr), .clk(sram_clk), .cs(dec_4x16_1_dec_out[13]),
    .rd_en(sram_rd), .memory_content(out_21), .data_out(controlled_buffer_1_out));
  sram_cell sram_cell_15 (
    .data_in(controlled_buffer_1_out), .wr_en(sram_wr), .clk(sram_clk), .cs(dec_4x16_1_dec_out[14]),
    .rd_en(sram_rd), .memory_content(out_22), .data_out(controlled_buffer_1_out));
  sram_cell sram_cell_16 (
    .data_in(controlled_buffer_1_out), .wr_en(sram_wr), .clk(sram_clk), .cs(dec_4x16_1_dec_out[15]),
    .rd_en(sram_rd), .memory_content(out_23), .data_out(controlled_buffer_1_out));
  assign sram_d_out = sram_rd ? controlled_buffer_1_out : 8'bz;  // Controlled_Buffer controlled_buffer_2
endmodule

module ins_reg (
  input  [7:0] ins_reg_in,
  input  ins_reg_in_en,
  input  clk,
  input  ins_reg_out_en,
  output [7:0] out_5,
  output [3:0] add_outs,
  output [3:0] ins_out
);

  reg_gp reg_gp_1 (
    .reg_in(ins_reg_in), .reg_in_en(ins_reg_in_en), .reg_clk(clk), .reg_int_out({ins_out, out_5[3:0]}));  // open: reg_out_en, reg_out
  assign add_outs = ins_reg_out_en ? out_5[3:0] : 4'bz;  // Controlled_Buffer controlled_buffer_1

  assign out_5[7:4] = ins_out;
endmodule

module cs (
  input  debug,
  input  clk,
  input  ring_reset,
  input  [3:0] data_in,
  input  [7:0] flag_reg,
  output pc_en,
  output pc_out,
  output pc_reset,
  output sram_wr,
  output [3:0] out_10,
  output sram_rd,
  output mar_in_en,
  output ins_reg_in_en,
  output ins_reg_out_en,
  output a_in,
  output a_out,
  output alu_out,
  output alu_sub,
  output b_in,
  output b_out,
  output ram_rd,
  output pc_in_en,
  output flag_clk
);

  wire and_1_out, and_2_out, and_3_out, and_4_out, and_5_out, and_6_out, and_7_out, and_8_out, and_9_out,
       and_10_out, and_11_out, and_12_out, and_13_out, and_14_out, and_15_out, and_16_out, and_17_out,
       and_18_out, and_19_out, and_20_out, and_21_out, and_22_out, and_23_out, and_24_out, and_25_out,
       and_26_out, and_27_out, and_28_out, and_29_out, and_30_out, and_31_out, and_32_out, and_33_out,
       and_34_out, and_35_out, and_36_out, and_37_out, and_38_out, and_39_out, and_40_out, and_41_out,
       and_42_out, and_43_out, and_44_out, and_45_out, and_46_out, and_48_out, and_49_out, and_50_out,
       and_51_out, and_52_out, controlled_buffer_1_out, demultiplexer_1_out0, nor_1_out, not_1_out,
       not_2_out, not_3_out, not_4_out, not_5_out, not_6_out, not_7_out, not_8_out, ring_reset_t,
       sram_wr_tunnel;
  wire [3:0] multiplexer_1_out, pull_resistor_1_node;
  wire [7:0] ring_counter_1_ring_out;
  wire [15:0] dec_4x16_1_dec_out;

  Pull_Resistor pull_resistor_1 (.node(pull_resistor_1_node));
  not not_1 (not_1_out, ring_reset);
  assign controlled_buffer_1_out = ring_reset ? ring_reset : 1'bz;  // Controlled_Buffer controlled_buffer_1
  Multiplexer #(.width(4)) multiplexer_1 (
    .in0(pull_resistor_1_node), .in1(data_in), .out(multiplexer_1_out), .sel(not_2_out));
  not not_2 (not_2_out, debug);
  assign controlled_buffer_1_out = not_1_out ? ring_reset_t : 1'bz;  // Controlled_Buffer controlled_buffer_2
  dec_4x16 dec_4x16_1 (.dec_sel(multiplexer_1_out), .dec_out(dec_4x16_1_dec_out));
  ring_counter ring_counter_1 (
    .clk(clk), .ring_reset(controlled_buffer_1_out), .ring_value(out_10), .ring_out(ring_counter_1_ring_out));
  not not_3 (not_3_out, flag_reg[0]);
  not not_4 (not_4_out, flag_reg[2]);
  not not_5 (not_5_out, flag_reg[0]);
  not not_6 (not_6_out, flag_reg[2]);
  not not_7 (not_7_out, flag_reg[0]);
  not not_8 (not_8_out, flag_reg[2]);
  and and_1 (and_1_out, dec_4x16_1_dec_out[1], ring_counter_1_ring_out[2]);
  and and_2 (and_2_out, dec_4x16_1_dec_out[2], ring_counter_1_ring_out[2]);
  and and_3 (and_3_out, ring_counter_1_ring_out[2], dec_4x16_1_dec_out[3]);
  and and_4 (and_4_out, ring_counter_1_ring_out[2], dec_4x16_1_dec_out[4]);
  and and_5 (and_5_out, ring_counter_1_ring_out[3], dec_4x16_1_dec_out[6]);
  and and_6 (and_6_out, ring_counter_1_ring_out[2], dec_4x16_1_dec_out[7]);
  and and_7 (and_7_out, ring_counter_1_ring_out[2], dec_4x16_1_dec_out[8]);
  and and_8 (and_8_out, dec_4x16_1_dec_out[1], ring_counter_1_ring_out[3]);
  and and_9 (and_9_out, dec_4x16_1_dec_out[2], ring_counter_1_ring_out[3]);
  and and_10 (and_10_out, dec_4x16_1_dec_out[6], ring_counter_1_ring_out[4]);
  and and_11 (and_11_out, dec_4x16_1_dec_out[8], ring_counter_1_ring_out[3]);
  and and_12 (and_12_out, dec_4x16_1_dec_out[1], ring_counter_1_ring_out[2]);
  and and_13 (and_13_out, dec_4x16_1_dec_out[2], ring_counter_1_ring_out[2]);
  and and_14 (and_14_out, dec_4x16_1_dec_out[3], ring_counter_1_ring_out[2]);
  and and_15 (and_15_out, dec_4x16_1_dec_out[4], ring_counter_1_ring_out[2]);
  and and_16 (and_16_out, dec_4x16_1_dec_out[7], ring_counter_1_ring_out[2]);
  and and_17 (and_17_out, ring_counter_1_ring_out[2], dec_4x16_1_dec_out[8]);
  and and_18 (and_18_out, ring_counter_1_ring_out[2], dec_4x16_1_dec_out[9]);
  and and_19 (and_19_out, ring_counter_1_ring_out[2], not_5_out, dec_4x16_1_dec_out[10]);
  and and_20 (and_20_out, ring_counter_1_ring_out[2], not_6_out, dec_4x16_1_dec_out[11]);
  and and_21 (and_21_out, dec_4x16_1_dec_out[1], ring_counter_1_ring_out[3]);
  and and_22 (and_22_out, ring_counter_1_ring_out[4], dec_4x16_1_dec_out[6]);
  and and_23 (and_23_out, dec_4x16_1_dec_out[1], ring_counter_1_ring_out[4]);
  and and_24 (and_24_out, dec_4x16_1_dec_out[2], ring_counter_1_ring_out[4]);
  and and_25 (and_25_out, ring_counter_1_ring_out[4], dec_4x16_1_dec_out[3]);
  and and_26 (and_26_out, dec_4x16_1_dec_out[4], ring_counter_1_ring_out[4]);
  and and_27 (and_27_out, ring_counter_1_ring_out[2], dec_4x16_1_dec_out[5]);
  and and_28 (and_28_out, dec_4x16_1_dec_out[0], ring_counter_1_ring_out[3]);
  and and_29 (and_29_out, ring_counter_1_ring_out[5], dec_4x16_1_dec_out[6]);
  and and_30 (and_30_out, dec_4x16_1_dec_out[7], ring_counter_1_ring_out[4]);
  and and_31 (and_31_out, ring_counter_1_ring_out[5], dec_4x16_1_dec_out[8]);
  and and_32 (and_32_out, ring_counter_1_ring_out[3], dec_4x16_1_dec_out[9]);
  and and_33 (and_33_out, ring_counter_1_ring_out[3], dec_4x16_1_dec_out[10]);
  and and_34 (and_34_out, ring_counter_1_ring_out[3], dec_4x16_1_dec_out[11]);
  and and_35 (and_35_out, dec_4x16_1_dec_out[10], not_3_out);
  and and_36 (and_36_out, dec_4x16_1_dec_out[11], not_4_out);
  and and_37 (and_37_out, dec_4x16_1_dec_out[2], ring_counter_1_ring_out[3]);
  and and_38 (and_38_out, dec_4x16_1_dec_out[8], ring_counter_1_ring_out[3]);
  and and_39 (and_39_out, dec_4x16_1_dec_out[3], ring_counter_1_ring_out[3]);
  and and_40 (and_40_out, dec_4x16_1_dec_out[4], ring_counter_1_ring_out[3]);
  and and_41 (and_41_out, dec_4x16_1_dec_out[7], ring_counter_1_ring_out[3]);
  and and_42 (and_42_out, dec_4x16_1_dec_out[3], ring_counter_1_ring_out[3]);
  and and_43 (and_43_out, dec_4x16_1_dec_out[4], ring_counter_1_ring_out[3]);
  and and_44 (and_44_out, dec_4x16_1_dec_out[4], ring_counter_1_ring_out[3]);
  and and_45 (and_45_out, ring_counter_1_ring_out[4], dec_4x16_1_dec_out[8]);
  and and_46 (and_46_out, ring_counter_1_ring_out[5], dec_4x16_1_dec_out[8]);
  and and_47 (a_out, dec_4x16_1_dec_out[7], ring_counter_1_ring_out[3]);
  and and_48 (and_48_out, dec_4x16_1_dec_out[8], ring_counter_1_ring_out[5]);
  and and_49 (and_49_out, dec_4x16_1_dec_out[9], ring_counter_1_ring_out[2]);
  and and_50 (and_50_out, dec_4x16_1_dec_out[10], not_7_out, ring_counter_1_ring_out[2]);
  and and_51 (and_51_out, dec_4x16_1_dec_out[11], not_8_out, ring_counter_1_ring_out[2]);
  and and_52 (and_52_out, dec_4x16_1_dec_out[6], ring_counter_1_ring_out[3]);
  Demultiplexer demultiplexer_1 (
    .out0(demultiplexer_1_out0), .out1(ram_rd), .in(ring_counter_1_ring_out[1]), .sel(debug));
  Demultiplexer demultiplexer_2 (
    .out0(ins_reg_in_en), .out1(sram_wr_tunnel), .in(ring_counter_1_ring_out[1]), .sel(debug));
  nor nor_1 (nor_1_out, dec_4x16_1_dec_out[5], dec_4x16_1_dec_out[9], and_35_out, and_36_out);
  or or_1 (pc_out, ring_counter_1_ring_out[0], and_52_out);
  or or_2 (ins_reg_out_en, and_19_out, and_17_out, and_12_out, and_14_out, and_16_out, and_15_out, and_13_out, and_18_out, and_20_out);
  or or_3 (a_in, and_21_out, and_22_out);
  or or_4 (b_in, and_37_out, and_38_out);
  or or_5 (sram_wr, and_39_out, and_41_out, sram_wr_tunnel, and_40_out);
  or or_6 (alu_out, and_42_out, and_43_out);
  or or_7 (alu_sub, and_44_out, and_46_out, and_45_out);
  buf or_8 (flag_clk, and_48_out);  // OR_Gate
  or or_9 (pc_in_en, and_49_out, and_51_out, and_50_out);
  or or_10 (mar_in_en, and_4_out, and_5_out, ring_counter_1_ring_out[0], and_2_out, and_3_out, and_1_out, and_6_out, and_7_out);
  or or_11 (sram_rd, demultiplexer_1_out0, and_9_out, and_10_out, and_11_out, and_8_out);
  and and_53 (pc_en, ring_counter_1_ring_out[2], nor_1_out);
  or or_12 (ring_reset_t, and_31_out, and_23_out, and_30_out, and_25_out, and_27_out, and_32_out, and_26_out, and_24_out, and_28_out, and_29_out, and_33_out, and_34_out);
  Pull_Resistor pull_resistor_2 (.node(b_out));

  // Notes on the sheet:
  //   S C O Z
  //   0. Debug
  //   1. LDA
  //   2. LDB
  //   3. OUT
  //   4. SUB
  //   5. HLT
  //   6. LDI
  //   7. STA
  //   8. CMP
  //   9. JMP
  //   10. JNZ
  //   11. JNC
endmodule

module ring_counter (
  input  clk,
  input  ring_reset,
  output [3:0] ring_value,
  output [7:0] ring_out
);

  wire controlled_buffer_1_out, not_1_out, pull_resistor_1_node;
  wire [3:0] pc_1_pc_out;
  wire [15:8] dec_4x16_1_dec_out;

  assign controlled_buffer_1_out = ring_reset ? ring_reset : 1'bz;  // Controlled_Buffer controlled_buffer_1
  not not_1 (not_1_out, ring_reset);
  Pull_Resistor #(.pull(1)) pull_resistor_1 (.node(pull_resistor_1_node));
  assign controlled_buffer_1_out = not_1_out ? ring_out[7] : 1'bz;  // Controlled_Buffer controlled_buffer_2
  pc pc_1 (
    .pc_en(pull_resistor_1_node), .pc_reset(controlled_buffer_1_out), .pc_clk(clk),
    .pc_out_en(pull_resistor_1_node), .pc_value(ring_value), .pc_out(pc_1_pc_out));  // open: pc_in, pc_in_en
  dec_4x16 dec_4x16_1 (.dec_sel(pc_1_pc_out), .dec_out({dec_4x16_1_dec_out, ring_out}));
endmodule

module copy (
  input  in_1,
  input  in_2,
  input  in_3,
  input  in_4,
  input  in_5,
  input  in_6,
  input  in_7,
  input  in_8,
  input  in_9,
  input  in_10,
  input  in_11,
  input  in_12,
  input  in_13,
  input  in_14,
  input  [7:0] in_15,
  input  in_16,
  input  in_17,
  output [7:0] out_18,
  output [3:0] out_19,
  output out_20,
  output [7:0] out_21,
  output [7:0] reg_0,
  output [7:0] reg_1,
  output [7:0] reg_2,
  output [7:0] reg_3,
  output [7:0] reg_4,
  output [7:0] reg_5,
  output [7:0] reg_6,
  output [7:0] reg_7,
  output [7:0] reg_8,
  output [7:0] reg_9,
  output [3:0] out_32,
  output [7:0] reg_10,
  output [3:0] out_34,
  output [7:0] reg_11,
  output [7:0] reg_12,
  output [3:0] out_37,
  output [7:0] reg_13,
  output [7:0] reg_14,
  output [7:0] reg_15,
  output [7:0] out_41
);

  wire [7:4] ins_reg_1_out_5;

  // pc_copy pc_copy_1: pin names not known; wires that end beside it: in_9, in_7, in_11, in_13, out_19, out_32
  sram sram_1 (
    .sram_d_in({out_41[7:4], out_32}), .sram_wr(in_1), .sram_rd(in_3), .mar_d_in({out_41[7:4], out_32}),
    .mar_in_en(in_5), .sram_clk(in_7), .sram_d_out({out_41[7:4], out_32}), .out_8(reg_0), .out_9(reg_1),
    .out_10(reg_2), .out_11(reg_3), .out_12(reg_4), .out_13(reg_5), .out_14(reg_6), .out_15(reg_7),
    .out_16(reg_8), .out_17(reg_9), .out_18(reg_10), .out_19(reg_11), .out_20(reg_12), .out_21(reg_13),
    .out_22(reg_14), .out_23(reg_15));
  assign {out_41[7:4], out_32} = in_17 ? in_15 : 8'bz;  // Controlled_Buffer controlled_buffer_1
  reg_gp reg_gp_1 (
    .reg_in({out_41[7:4], out_32}), .reg_in_en(in_6), .reg_clk(in_7), .reg_out_en(in_8),
    .reg_int_out(out_18), .reg_out({out_41[7:4], out_32}));
  reg_gp reg_gp_2 (
    .reg_in({out_41[7:4], out_32}), .reg_in_en(in_10), .reg_clk(in_7), .reg_out_en(in_12),
    .reg_int_out(out_21), .reg_out({out_41[7:4], out_32}));
  ins_reg ins_reg_1 (
    .ins_reg_in({out_41[7:4], out_32}), .ins_reg_in_en(in_2), .clk(in_7), .ins_reg_out_en(in_4),
    .out_5({ins_reg_1_out_5, out_32}), .add_outs(out_34));  // open: ins_out
  alu alu_1 (
    .alu_in_1(out_18), .alu_out_en(in_14), .alu_sub(in_16), .alu_in_2(out_21), .alu_zero_out(out_20),
    .alu_overflow_out(out_32[0]));  // open: alu_carry_out, alu_out, alu_sign_out
  // cs cs_1: pin names not known; wires that end beside it: in_7, out_34, in_9, in_13, in_11, out_37, in_1, in_3, in_5, in_2, in_4, in_6, in_8, in_14, in_16, in_10, in_12
  // Pins of 4 and 8 bits meet at {ins_reg_1_out_5, out_32}
  // Pins of 1 and 8 bits meet at {out_41[7:4], out_32}

  assign out_41[3:0] = out_32;

  // Other names for the same wires on the sheet: a_in = in_6; a_out = in_8; alu_out = in_14; alu_sub = in_16;
  //   b_in = in_10; b_out = in_12; clk = in_7; debug = in_17; debug_data[7:0] = in_15; ins_reg_in_en = in_2;
  //   ins_reg_out_en = in_4; mar_in_en = in_5; pc_en = in_9; pc_out = in_13; pc_reset = in_11; sram_rd = in_3;
  //   sram_wr = in_1

  // Notes on the sheet:
  //   Clock
  //   RAM control
  //   PC control
  //   Debug & Testing
  //   IR control
  //   Register A control
  //   Register B control
  //   ALU control
endmodule

module copy2 (
  input  in_1,
  input  in_2,
  input  [7:0] in_3,
  input  in_4,
  input  in_5,
  input  in_6,
  input  [7:0] in_7,
  input  in_8,
  output [7:0] out_9,
  output [3:0] out_10,
  output out_11,
  output [3:0] out_12,
  output [7:0] out_13,
  output [7:0] out_14,
  output [7:0] out_15,
  output [3:0] out_16,
  output [3:0] out_17,
  output [3:0] out_18,
  output [7:0] out_19
);

  wire a_in, a_out, alu_out, alu_sub, b_in, b_out, clk, ins_reg_in_en, ins_reg_out_en, mar_in_en, pc_en,
       pc_out, sram_rd, sram_wr;
  wire [7:0] ram_1_dout;
  wire [7:4] reg_gp_1_reg_int_out;

  reg_gp reg_gp_1 (
    .reg_in(out_14), .reg_in_en(mar_in_en), .reg_clk(clk), .reg_int_out({reg_gp_1_reg_int_out, out_12}));  // open: reg_out_en, reg_out
  RAM #(.addrWidth(4), .trigger("falling")) ram_1 (
    .addr(out_12), .we(sram_wr), .oe(sram_rd), .clk(clk), .din(out_14), .dout(ram_1_dout));
  // pc_copy pc_copy_1: pin names not known; wires that end beside it: pc_en, clk, in_1, pc_out, out_10, out_14[3:0]
  assign out_14 = sram_rd ? ram_1_dout : 8'bz;  // Controlled_Buffer controlled_buffer_1
  assign out_14 = in_4 ? in_3 : 8'bz;  // Controlled_Buffer controlled_buffer_2
  Clock clock_1 (.out(clk));
  reg_gp reg_gp_2 (
    .reg_in(out_14), .reg_in_en(a_in), .reg_clk(clk), .reg_out_en(a_out), .reg_int_out(out_9),
    .reg_out(out_14));
  reg_gp reg_gp_3 (
    .reg_in(out_14), .reg_in_en(b_in), .reg_clk(clk), .reg_out_en(b_out), .reg_int_out(out_13),
    .reg_out(out_14));
  ins_reg ins_reg_1 (
    .ins_reg_in(out_14), .ins_reg_in_en(ins_reg_in_en), .clk(clk), .ins_reg_out_en(ins_reg_out_en),
    .out_5(out_15), .add_outs(out_14[3:0]), .ins_out(out_17));
  alu alu_1 (
    .alu_in_1(out_9), .alu_out_en(alu_out), .alu_sub(alu_sub), .alu_in_2(out_13), .alu_zero_out(out_11),
    .alu_overflow_out(out_14[0]));  // open: alu_carry_out, alu_out, alu_sign_out
  // cs cs_1: pin names not known; wires that end beside it: clk, in_2, out_17, pc_en, pc_out, in_1, sram_wr, out_18, sram_rd, mar_in_en, ins_reg_in_en, ins_reg_out_en, a_in, a_out, alu_out, alu_sub, b_in, b_out
  // Pins of 1 and 8 bits meet at out_14

  assign out_16 = out_14[3:0];
  assign out_19 = out_14;

  // Other names for the same wires on the sheet: debug = in_4; debug_data[7:0] = in_3; pc_reset = in_1;
  //   ring_reset = in_2

  // Notes on the sheet:
  //   Clock
  //   Debug & Testing
endmodule

module pc (
  input  pc_en,
  input  [3:0] pc_in,
  input  pc_in_en,
  input  pc_reset,
  input  pc_clk,
  input  pc_out_en,
  output [3:0] pc_value,
  output [3:0] pc_out
);

  wire and_1_out, and_2_out, and_3_out, multiplexer_1_out, multiplexer_2_out, multiplexer_3_out,
       multiplexer_4_out, multiplexer_5_out, multiplexer_6_out, multiplexer_7_out, multiplexer_8_out,
       not_1_out, not_2_out, not_3_out, not_4_out;

  Multiplexer multiplexer_1 (.in0(and_1_out), .in1(not_1_out), .out(multiplexer_1_out), .sel(pc_in_en));
  and and_1 (and_1_out, pc_en, pc_value[2], pc_value[1], pc_value[0]);
  not not_1 (not_1_out, pc_in[3]);
  Multiplexer multiplexer_2 (.in0(and_1_out), .in1(pc_in[3]), .out(multiplexer_2_out), .sel(pc_in_en));
  J_K_Flip_Flop j_k_ff_1 (
    .J(multiplexer_2_out), .K(multiplexer_1_out), .clk(pc_clk), .Q(pc_value[3]), .reset(pc_reset));  // open: Qn, preset
  and and_2 (and_2_out, pc_en, pc_value[1], pc_value[0]);
  Multiplexer multiplexer_3 (.in0(and_2_out), .in1(pc_in[2]), .out(multiplexer_3_out), .sel(pc_in_en));
  Multiplexer multiplexer_4 (.in0(and_2_out), .in1(not_2_out), .out(multiplexer_4_out), .sel(pc_in_en));
  J_K_Flip_Flop j_k_ff_2 (
    .J(multiplexer_3_out), .K(multiplexer_4_out), .clk(pc_clk), .Q(pc_value[2]), .reset(pc_reset));  // open: Qn, preset
  not not_2 (not_2_out, pc_in[2]);
  and and_3 (and_3_out, pc_en, pc_value[0]);
  Multiplexer multiplexer_5 (.in0(and_3_out), .in1(pc_in[1]), .out(multiplexer_5_out), .sel(pc_in_en));
  not not_3 (not_3_out, pc_in[1]);
  Multiplexer multiplexer_6 (.in0(and_3_out), .in1(not_3_out), .out(multiplexer_6_out), .sel(pc_in_en));
  J_K_Flip_Flop j_k_ff_3 (
    .J(multiplexer_5_out), .K(multiplexer_6_out), .clk(pc_clk), .Q(pc_value[1]), .reset(pc_reset));  // open: Qn, preset
  J_K_Flip_Flop j_k_ff_4 (
    .J(multiplexer_7_out), .K(multiplexer_8_out), .clk(pc_clk), .Q(pc_value[0]), .reset(pc_reset));  // open: Qn, preset
  not not_4 (not_4_out, pc_in[0]);
  Multiplexer multiplexer_7 (.in0(pc_en), .in1(pc_in[0]), .out(multiplexer_7_out), .sel(pc_in_en));
  Multiplexer multiplexer_8 (.in0(pc_en), .in1(not_4_out), .out(multiplexer_8_out), .sel(pc_in_en));
  assign pc_out = pc_out_en ? pc_value : 4'bz;  // Controlled_Buffer controlled_buffer_1
endmodule

module test (
  input  in_1,
  input  [3:0] in_2,
  output pc_out,
  output mar_in,
  output sram_rd,
  output ins_in_en,
  output ins_out_en,
  output a_in,
  output pc_en,
  output ring_reset
);

  wire and_1_out, and_2_out, and_3_out;
  wire [7:1] ring_counter_1_ring_out;
  wire [15:0] dec_4x16_1_dec_out;

  dec_4x16 dec_4x16_1 (.dec_sel(in_2), .dec_out(dec_4x16_1_dec_out));
  ring_counter ring_counter_1 (
    .clk(in_1), .ring_reset(ring_reset), .ring_out({ring_counter_1_ring_out, pc_out}));  // open: ring_value
  and and_1 (and_1_out, ring_counter_1_ring_out[2], dec_4x16_1_dec_out[0]);
  and and_2 (and_2_out, ring_counter_1_ring_out[1], dec_4x16_1_dec_out[0]);
  and and_3 (and_3_out, ring_counter_1_ring_out[3], dec_4x16_1_dec_out[0]);
  or or_1 (mar_in, pc_out, and_1_out);
  or or_2 (sram_rd, and_2_out, and_3_out);
  and and_4 (ins_in_en, ring_counter_1_ring_out[1], dec_4x16_1_dec_out[0]);
  and and_5 (ins_out_en, ring_counter_1_ring_out[2], dec_4x16_1_dec_out[0]);
  and and_6 (a_in, ring_counter_1_ring_out[3], dec_4x16_1_dec_out[0]);
  and and_7 (pc_en, ring_counter_1_ring_out[3], dec_4x16_1_dec_out[0]);
  and and_8 (ring_reset, ring_counter_1_ring_out[4], dec_4x16_1_dec_out[0]);
endmodule
